// Logisim project ControlSystem.circ as structural Verilog: 8 circuits, main circuit Reg
module Reg (
  input  [7:0] data,
  input  [1:0] C_Reg,
  input  R_W,
  input  CLK,
  input  [1:0] SA,
  input  [1:0] SB,
  output [7:0] A_tunnel,
  output [7:0] B_tunnel
);

  wire and_1_out, and_2_out, and_3_out, and_4_out, decoder_1_out0, decoder_1_out1, decoder_1_out2,
       decoder_1_out3;
  wire [7:0] R0_q, R1_q, R2_q, R3_q;

  Decoder #(.select(2)) decoder_1 (
    .out0(decoder_1_out0), .out1(decoder_1_out1), .out2(decoder_1_out2), .out3(decoder_1_out3), .sel(C_Reg));  // open: en
  // Probe on data
  and and_1 (and_1_out, decoder_1_out0, R_W);
  and and_2 (and_2_out, decoder_1_out1, R_W);
  and and_3 (and_3_out, decoder_1_out2, R_W);
  and and_4 (and_4_out, decoder_1_out3, R_W);
  Register R0 (.D(data), .en(and_1_out), .Q(R0_q), .clk(CLK));  // open: clr
  Register R1 (.D(data), .en(and_2_out), .Q(R1_q), .clk(CLK));  // open: clr
  Register R2 (.D(data), .en(and_3_out), .Q(R2_q), .clk(CLK));  // open: clr
  Register R3 (.D(data), .en(and_4_out), .Q(R3_q), .clk(CLK));  // open: clr
  Multiplexer #(.select(2), .width(8)) multiplexer_1 (
    .in0(R0_q), .in1(R1_q), .in2(R2_q), .in3(R3_q), .out(A_tunnel), .sel(SA));  // open: en
  Multiplexer #(.select(2), .width(8)) multiplexer_2 (
    .in0(R0_q), .in1(R1_q), .in2(R2_q), .in3(R3_q), .out(B_tunnel), .sel(SB));  // open: en
endmodule

module ProgramCounter (
  input  \TC切到下一指令 ,
  input  RST,
  input  [7:0] \偏移量 ,
  input  sel,
  output [7:0] P_address
);

  wire [7:0] adder_1_out, multiplexer_1_out;

  Register register_1 (.D(adder_1_out), .Q(P_address), .clk(\TC切到下一指令 ), .clr(RST));  // open: en
  Multiplexer #(.width(8)) multiplexer_1 (.in0(8'h1), .in1(\偏移量 ), .out(multiplexer_1_out), .sel(sel));  // open: en
  Adder adder_1 (.a(P_address), .b(multiplexer_1_out), .out(adder_1_out));  // open: cin, cout

  // Notes on the sheet:
  //   sel==0默认加1
endmodule

module IR_TD (
  input  [15:0] \I_in指令入口 ,
  input  \TF取值使能 ,
  output \R_W读或写 ,
  output \S_B_I选择B或者立即数 ,
  output \RM读内存 ,
  output \WM写内存 ,
  output JP,
  output JZ,
  output JC,
  output [4:0] \S_op运算选择 ,
  output [7:0] \S_Regs选择寄存器 
);

  wire [15:13] register_1_q;

  Register #(.width(16)) register_1 (
    .D(\I_in指令入口 ), .Q({register_1_q, \S_op运算选择 , \S_Regs选择寄存器 }), .clk(\TF取值使能 ));  // open: en, clr
  Ctrl3x7decoder ctrl3x7decoder_1 (
    .H(register_1_q[15]), .M(register_1_q[14]), .L(register_1_q[13]), .\RW读或写 (\R_W读或写 ),
    .\SBI选择B或者立即数 (\S_B_I选择B或者立即数 ), .\RM读内存 (\RM读内存 ), .\WM写内存 (\WM写内存 ), .JP(JP), .JZ(JZ), .JC(JC));

  // Notes on the sheet:
  //   IR指令储存器
endmodule

module Ctrl3x7decoder (
  input  H,
  input  M,
  input  L,
  output \RW读或写 ,
  output \SBI选择B或者立即数 ,
  output \RM读内存 ,
  output \WM写内存 ,
  output JP,
  output JZ,
  output JC
);

  wire and_1_out, and_2_out, and_3_out, and_4_out, and_5_out, and_6_out, and_7_out, and_8_out, and_9_out,
       not_1_out, not_2_out, not_3_out, not_4_out, not_5_out, not_6_out, not_7_out, not_8_out, not_9_out,
       not_10_out, not_11_out, not_12_out;

  not not_1 (not_1_out, H);
  not not_2 (not_2_out, M);
  not not_3 (not_3_out, H);
  not not_4 (not_4_out, M);
  not not_5 (not_5_out, L);
  not not_6 (not_6_out, H);
  not not_7 (not_7_out, H);
  not not_8 (not_8_out, M);
  not not_9 (not_9_out, M);
  and and_1 (and_1_out, H, M);
  not not_10 (not_10_out, L);
  and and_2 (and_2_out, not_1_out, not_2_out);
  and and_3 (and_3_out, not_3_out, L);
  and and_4 (and_4_out, not_4_out, L);
  and and_5 (and_5_out, H, not_5_out);
  and and_6 (and_6_out, not_6_out, M);
  and and_7 (and_7_out, not_7_out, M);
  not not_11 (not_11_out, L);
  and and_8 (and_8_out, H, not_8_out);
  not not_12 (not_12_out, L);
  and and_9 (and_9_out, H, not_9_out);
  and and_10 (JC, and_1_out, not_10_out);
  or or_1 (\RW读或写 , and_2_out, and_3_out);
  or or_2 (\SBI选择B或者立即数 , and_4_out, and_5_out);
  and and_11 (\RM读内存 , and_6_out, L);
  and and_12 (\WM写内存 , and_7_out, not_11_out);
  and and_13 (JP, and_8_out, not_12_out);
  and and_14 (JZ, and_9_out, L);
endmodule

module CLK (
  input  CLK,
  input  Reset,
  output T0,
  output T1,
  output T2,
  output T3
);

  wire [1:0] counter_1_q;

  Counter #(.width(2), .max('h3)) counter_1 (.Q(counter_1_q), .clk(CLK), .clr(Reset));  // open: load, D, count, carry
  Decoder #(.select(2)) decoder_1 (.out0(T0), .out1(T1), .out2(T2), .out3(T3), .sel(counter_1_q));  // open: en
endmodule

module S_B_I (
  input  [7:0] \B通道输出 ,
  input  [3:0] \_4位立即数 ,
  input  \S_B_I选择数 ,
  output [7:0] \加法器B通道输入 
);

  wire [7:0] bit_extender_1_out;

  // Probe on \_4位立即数 
  assign bit_extender_1_out = {{4{\_4位立即数 [3]}}, \_4位立即数 };  // Bit_Extender bit_extender_1
  Multiplexer #(.width(8)) multiplexer_1 (
    .in0(\B通道输出 ), .in1(bit_extender_1_out), .out(\加法器B通道输入 ), .sel(\S_B_I选择数 ));  // open: en
  // Probe on \加法器B通道输入 
endmodule

module C_U (
  input  \TC切换下一 ,
  input  RST,
  input  O,
  input  S,
  input  C,
  input  Z,
  input  \TA执行指令 ,
  input  [15:0] \I_in指令入口 ,
  input  \TF取值使能 ,
  output [7:0] P_address,
  output \R_W读或写 ,
  output \S_B_I选择B或者立即数 ,
  output \RM读内存 ,
  output \WM写内存 ,
  output JP,
  output JZ,
  output JC,
  output [4:0] \S_op运算选择 ,
  output [7:0] ADDRIM
);

  wire and_1_out, multiplexer_1_out;
  wire [3:0] register_1_q;

  Register #(.width(4)) register_1 (.D({Z, C, S, O}), .Q(register_1_q), .clk(\TA执行指令 ));  // open: en, clr
  Multiplexer #(.select(3), .enable("false")) multiplexer_1 (
    .in0(1'b1), .in1(register_1_q[0]), .in2(register_1_q[1]), .in3(register_1_q[2]), .in4(register_1_q[3]),
    .out(multiplexer_1_out), .sel(\S_op运算选择 [4:2]));  // open: in5, in6, in7
  and and_1 (and_1_out, multiplexer_1_out, \R_W读或写 );
  IR_TD ir_td_1 (
    .\I_in指令入口 (\I_in指令入口 ), .\TF取值使能 (\TF取值使能 ), .\R_W读或写 (\R_W读或写 ), .\S_B_I选择B或者立即数 (\S_B_I选择B或者立即数 ),
    .\RM读内存 (\RM读内存 ), .\WM写内存 (\WM写内存 ), .JP(JP), .JZ(JZ), .JC(JC), .\S_op运算选择 (\S_op运算选择 ),
    .\S_Regs选择寄存器 (ADDRIM));
  ProgramCounter programcounter_1 (
    .\TC切到下一指令 (\TC切换下一 ), .RST(RST), .\偏移量 (ADDRIM), .sel(and_1_out), .P_address(P_address));

  // Other names for the same wires on the sheet: OPCODE[4:0] = \S_op运算选择 
endmodule

module Controller (
  input  in_1,
  input  \Reset_重启 
);

  wire clock_1_out, cu_1_p8, cu_1_p9, cu_1_p10, decoder_1_out0, decoder_1_out1, decoder_1_out2,
       decoder_1_out3, regs_1_p3;
  wire [1:0] counter_1_q, cu_1_p12, regs_1_p2, regs_1_p5, regs_1_p6;
  wire [4:0] cu_1_p11;
  wire [7:0] bit_extender_1_out, cu_1_p6, functionunit_1_p7, multiplexer_1_out, ram_1_data, regs_1_p1,
       regs_1_p7, regs_1_p8;
  wire [15:0] rom_1_data;

  Clock clock_1 (.out(clock_1_out));
  // Probe on cu_1_p6
  Decoder #(.select(2), .enable("false")) decoder_1 (
    .out0(decoder_1_out0), .out1(decoder_1_out1), .out2(decoder_1_out2), .out3(decoder_1_out3),
    .sel(counter_1_q));
  Counter #(.width(2), .max('h3)) counter_1 (
    .Q(counter_1_q), .clk(clock_1_out), .clr(\Reset_重启 ));  // open: load, D, count, carry
  ROM #(.dataWidth(16)) rom_1 (.addr(cu_1_p6), .data(rom_1_data), .sel(1'b1));
  // Probe on rom_1_data
  // Probe on regs_1_p1
  // Probe on regs_1_p7
  // Probe on multiplexer_1_out
  // Regs regs_1: pin names not known; wires that end beside it: regs_1_p1, regs_1_p2, regs_1_p3, decoder_1_out3, regs_1_p5, regs_1_p6, regs_1_p7, regs_1_p8
  assign bit_extender_1_out = {{4{1'b0}}, {regs_1_p6, cu_1_p12}};  // Bit_Extender bit_extender_1
  // CU cu_1: pin names not known; wires that end beside it: \Reset_重启 , decoder_1_out0, rom_1_data, decoder_1_out1, decoder_1_out3, cu_1_p6, regs_1_p3, cu_1_p8, cu_1_p9, cu_1_p10, cu_1_p11, {regs_1_p2, regs_1_p5, regs_1_p6, cu_1_p12}
  // Probe on {regs_1_p2, regs_1_p5, regs_1_p6, cu_1_p12}
  Multiplexer #(.width(8), .enable("false")) multiplexer_1 (
    .in0(regs_1_p8), .in1(bit_extender_1_out), .out(multiplexer_1_out), .sel(cu_1_p8));
  RAM #(.bus("separate")) ram_1 (
    .addr(regs_1_p7), .din(multiplexer_1_out), .data(ram_1_data), .str(cu_1_p10), .sel(1'b1),
    .clk(decoder_1_out2), .ld(1'b1), .clr(in_1));
  // FunctionUnit functionunit_1: pin names not known; wires that end beside it: regs_1_p7, multiplexer_1_out, cu_1_p11[0], cu_1_p11[2:1], cu_1_p11[3], cu_1_p11[4], functionunit_1_p7
  Multiplexer #(.width(8), .enable("false")) multiplexer_2 (
    .in0(functionunit_1_p7), .in1(ram_1_data), .out(regs_1_p1), .sel(cu_1_p9));
  ROM #(.dataWidth(16)) rom_2 ();  // open: addr, data, sel
  ROM #(.dataWidth(16)) rom_3 ();  // open: addr, data, sel

  // Notes on the sheet:
  //   contents of rom_1 (hex, n*v repeats v):
  //   2001 2041 20c0 1084 4038 15f0 4 48 80fb
  //   -8*10
  //   -8/4
  //   contents of rom_2 (hex, n*v repeats v):
  //   2008 600 600 4000 12*0 1010
  //   contents of rom_3 (hex, n*v repeats v):
  //   2008 40 20c0 200 244 244 244 1084 4038 7*0 1010
endmodule
