// Logisim project exp2.circ as structural Verilog: 15 circuits, main circuit 3x8decoder
module _3x8decoder (
  input  In0,
  input  In1,
  input  In2,
  output Out0,
  output Out1,
  output Out2,
  output Out3,
  output Out4,
  output Out5,
  output Out6,
  output Out7
);

  wire not_1_out, not_2_out, not_3_out, not_4_out, not_5_out, not_6_out, not_7_out, not_8_out, not_9_out,
       not_10_out, not_11_out, not_12_out;

  not not_1 (not_1_out, In0);
  not not_2 (not_2_out, In1);
  not not_3 (not_3_out, In2);
  not not_4 (not_4_out, In0);
  not not_5 (not_5_out, In1);
  not not_6 (not_6_out, In0);
  not not_7 (not_7_out, In2);
  not not_8 (not_8_out, In0);
  not not_9 (not_9_out, In1);
  not not_10 (not_10_out, In2);
  not not_11 (not_11_out, In1);
  not not_12 (not_12_out, In2);
  and and_1 (Out7, In0, In1, In2);
  and and_2 (Out0, not_1_out, not_2_out, not_3_out);
  and and_3 (Out1, not_4_out, not_5_out, In2);
  and and_4 (Out2, not_6_out, In1, not_7_out);
  and and_5 (Out3, not_8_out, In1, In2);
  and and_6 (Out4, In0, not_9_out, not_10_out);
  and and_7 (Out5, In0, not_11_out, In2);
  and and_8 (Out6, In0, In1, not_12_out);
endmodule

module _1bit_half_adder (
  input  A,
  input  B,
  output S,
  output C
);

  wire and_2_out, and_3_out, not_1_out, not_2_out;

  not not_1 (not_1_out, A);
  not not_2 (not_2_out, B);
  and and_1 (C, A, B);
  and and_2 (and_2_out, not_1_out, B);
  and and_3 (and_3_out, A, not_2_out);
  or or_1 (S, and_2_out, and_3_out);
endmodule

module _1bit_full_adder (
  input  A,
  input  B,
  input  Cin,
  output Cout,
  output S
);

  wire and_1_out, and_2_out, and_3_out, and_4_out, and_5_out, and_6_out, and_7_out, not_1_out, not_2_out,
       not_3_out, not_4_out, not_5_out, not_6_out;

  and and_1 (and_1_out, B, Cin);
  and and_2 (and_2_out, A, Cin);
  and and_3 (and_3_out, A, B);
  not not_1 (not_1_out, A);
  not not_2 (not_2_out, B);
  not not_3 (not_3_out, A);
  not not_4 (not_4_out, Cin);
  not not_5 (not_5_out, B);
  not not_6 (not_6_out, Cin);
  or or_1 (Cout, and_1_out, and_2_out, and_3_out);
  and and_4 (and_4_out, not_1_out, not_2_out, Cin);
  and and_5 (and_5_out, not_3_out, B, not_4_out);
  and and_6 (and_6_out, A, not_5_out, not_6_out);
  and and_7 (and_7_out, A, B, Cin);
  or or_2 (S, and_4_out, and_5_out, and_6_out, and_7_out);
endmodule

module _1bit_full_substracter (
  input  Xi,
  input  Yi,
  input  Bi,
  output Di,
  output Bi_2
);

  wire and_1_out, and_2_out, and_3_out, and_4_out, and_5_out, and_6_out, and_7_out, not_1_out, not_2_out,
       not_3_out, not_4_out, not_5_out, not_6_out, not_7_out, not_8_out;

  not not_1 (not_1_out, Xi);
  not not_2 (not_2_out, Yi);
  not not_3 (not_3_out, Xi);
  not not_4 (not_4_out, Bi);
  not not_5 (not_5_out, Yi);
  not not_6 (not_6_out, Bi);
  not not_7 (not_7_out, Xi);
  not not_8 (not_8_out, Xi);
  and and_1 (and_1_out, not_1_out, not_2_out, Bi);
  and and_2 (and_2_out, not_3_out, Yi, not_4_out);
  and and_3 (and_3_out, Xi, not_5_out, not_6_out);
  and and_4 (and_4_out, Xi, Yi, Bi);
  and and_5 (and_5_out, not_7_out, Bi);
  and and_6 (and_6_out, not_8_out, Yi);
  and and_7 (and_7_out, Yi, Bi);
  or or_1 (Di, and_1_out, and_2_out, and_3_out, and_4_out);
  or or_2 (Bi_2, and_5_out, and_6_out, and_7_out);
endmodule

module _4bit_full_adder (
  input  A0,
  input  B0,
  input  C,
  input  A1,
  input  B1,
  input  A2,
  input  B2,
  input  A3,
  input  B3,
  output S0,
  output S1,
  output S2,
  output C3,
  output S3
);

  wire n1bit_full_adder_1_cout, n1bit_full_adder_2_cout, n1bit_full_adder_3_cout;

  _1bit_full_adder u_1bit_full_adder_1 (.A(A0), .B(B0), .Cin(C), .Cout(n1bit_full_adder_1_cout), .S(S0));
  _1bit_full_adder u_1bit_full_adder_2 (
    .A(A1), .B(B1), .Cin(n1bit_full_adder_1_cout), .Cout(n1bit_full_adder_2_cout), .S(S1));
  _1bit_full_adder u_1bit_full_adder_3 (
    .A(A2), .B(B2), .Cin(n1bit_full_adder_2_cout), .Cout(n1bit_full_adder_3_cout), .S(S2));
  _1bit_full_adder u_1bit_full_adder_4 (.A(A3), .B(B3), .Cin(n1bit_full_adder_3_cout), .Cout(C3), .S(S3));

  // Notes on the sheet:
  //   C0
  //   C1
  //   C2
  //   C3
endmodule

module _4bit_full_substracter (
  input  X0,
  input  Y0,
  input  B,
  input  X1,
  input  Y1,
  input  X2,
  input  Y2,
  input  X3,
  input  Y3,
  output D0,
  output D1,
  output D2,
  output D3,
  output B3
);

  wire n1bit_full_substracter_1_bi_2, n1bit_full_substracter_2_bi_2, n1bit_full_substracter_3_bi_2;

  _1bit_full_substracter u_1bit_full_substracter_1 (
    .Xi(X0), .Yi(Y0), .Bi(B), .Di(D0), .Bi_2(n1bit_full_substracter_1_bi_2));
  _1bit_full_substracter u_1bit_full_substracter_2 (
    .Xi(X1), .Yi(Y1), .Bi(n1bit_full_substracter_1_bi_2), .Di(D1), .Bi_2(n1bit_full_substracter_2_bi_2));
  _1bit_full_substracter u_1bit_full_substracter_3 (
    .Xi(X2), .Yi(Y2), .Bi(n1bit_full_substracter_2_bi_2), .Di(D2), .Bi_2(n1bit_full_substracter_3_bi_2));
  _1bit_full_substracter u_1bit_full_substracter_4 (
    .Xi(X3), .Yi(Y3), .Bi(n1bit_full_substracter_3_bi_2), .Di(D3), .Bi_2(B3));
endmodule

module _8bit_full_adder (
  input  Cin,
  input  A0,
  input  A4,
  input  A1,
  input  A5,
  input  A2,
  input  A6,
  input  A3,
  input  A7,
  input  B0,
  input  B1,
  input  B2,
  input  B3,
  input  B4,
  input  B5,
  input  B6,
  input  B7,
  output S0,
  output S4,
  output S1,
  output S5,
  output S2,
  output S6,
  output S3,
  output S7,
  output Cout,
  output Overflow
);

  wire n4bit_full_adder_1_c3, xnor_1_out, xor_1_out;

  _4bit_full_adder u_4bit_full_adder_1 (
    .A0(A0), .B0(B0), .C(Cin), .A1(A1), .B1(B1), .A2(A2), .B2(B2), .A3(A3), .B3(B3), .S0(S0), .S1(S1),
    .S2(S2), .C3(n4bit_full_adder_1_c3), .S3(S3));
  _4bit_full_adder u_4bit_full_adder_2 (
    .A0(A4), .B0(B4), .C(n4bit_full_adder_1_c3), .A1(A5), .B1(B5), .A2(A6), .B2(B6), .A3(A7), .B3(B7),
    .S0(S4), .S1(S5), .S2(S6), .C3(Cout), .S3(S7));
  xor xor_1 (xor_1_out, S7, A7);
  xnor xnor_1 (xnor_1_out, B7, A7);
  and and_1 (Overflow, xor_1_out, xnor_1_out);
endmodule

module _8bit_full_substracter (
  input  Bin,
  input  X0,
  input  X4,
  input  X1,
  input  X5,
  input  X2,
  input  X6,
  input  X3,
  input  X7,
  input  Y0,
  input  Y1,
  input  Y2,
  input  Y3,
  input  Y4,
  input  Y5,
  input  Y6,
  input  Y7,
  output D0,
  output D4,
  output D1,
  output D5,
  output D2,
  output D6,
  output D3,
  output D7,
  output Bout
);

  wire n4bit_full_substracter_1_b3;

  _4bit_full_substracter u_4bit_full_substracter_1 (
    .X0(X0), .Y0(Y0), .B(Bin), .X1(X1), .Y1(Y1), .X2(X2), .Y2(Y2), .X3(X3), .Y3(Y3), .D0(D0), .D1(D1),
    .D2(D2), .D3(D3), .B3(n4bit_full_substracter_1_b3));
  _4bit_full_substracter u_4bit_full_substracter_2 (
    .X0(X4), .Y0(Y4), .B(n4bit_full_substracter_1_b3), .X1(X5), .Y1(Y5), .X2(X6), .Y2(Y6), .X3(X7), .Y3(Y7),
    .D0(D4), .D1(D5), .D2(D6), .D3(D7), .B3(Bout));
endmodule

module _16bit_full_adder (
  input  Cin,
  input  A0,
  input  A8,
  input  A1,
  input  A9,
  input  A2,
  input  A10,
  input  A3,
  input  A11,
  input  A4,
  input  A12,
  input  A5,
  input  A13,
  input  A6,
  input  A14,
  input  A7,
  input  A15,
  input  B0,
  input  B1,
  input  B2,
  input  B3,
  input  B4,
  input  B5,
  input  B6,
  input  B7,
  input  B8,
  input  B9,
  input  B10,
  input  B11,
  input  B12,
  input  B13,
  input  B14,
  input  B15,
  output S0,
  output S8,
  output S1,
  output S9,
  output S2,
  output S10,
  output S3,
  output S11,
  output S4,
  output S12,
  output S5,
  output S13,
  output S6,
  output S14,
  output S7,
  output S15,
  output Cout,
  output Overflow
);

  wire n8bit_full_adder_1_cout;

  _8bit_full_adder u_8bit_full_adder_1 (
    .Cin(Cin), .A0(A0), .A4(A1), .A1(A2), .A5(A3), .A2(A4), .A6(A5), .A3(A6), .A7(A7), .S0(S0), .S4(S1),
    .S1(S2), .S5(S3), .S2(S4), .S6(S5), .S3(S6), .S7(S7), .Cout(n8bit_full_adder_1_cout), .B0(B0), .B1(B1),
    .B2(B2), .B3(B3), .B4(B4), .B5(B5), .B6(B6), .B7(B7));  // open: Overflow
  _8bit_full_adder u_8bit_full_adder_2 (
    .Cin(n8bit_full_adder_1_cout), .A0(A8), .A4(A9), .A1(A10), .A5(A11), .A2(A12), .A6(A13), .A3(A14),
    .A7(A15), .S0(S8), .S4(S9), .S1(S10), .S5(S11), .S2(S12), .S6(S13), .S3(S14), .S7(S15), .Cout(Cout),
    .Overflow(Overflow), .B0(B8), .B1(B9), .B2(B10), .B3(B11), .B4(B12), .B5(B13), .B6(B14), .B7(B15));
endmodule

module CLA74182 (
  input  Cin,
  input  G1,
  input  G2,
  input  G3,
  input  G4,
  input  P1,
  input  P2,
  input  P3,
  input  P4,
  output C1,
  output C2,
  output C3,
  output C4,
  output P,
  output G
);

  wire and_1_out, and_2_out, and_3_out, and_4_out, and_5_out, and_6_out, and_7_out, and_8_out, and_9_out,
       and_10_out, and_12_out, and_13_out, and_14_out;

  and and_1 (and_1_out, P1, Cin);
  and and_2 (and_2_out, P2, G1);
  and and_3 (and_3_out, P2, P1, Cin);
  and and_4 (and_4_out, P3, G2);
  and and_5 (and_5_out, P3, P2, G1);
  and and_6 (and_6_out, P3, P2, P1, Cin);
  and and_7 (and_7_out, P4, G3);
  and and_8 (and_8_out, P4, P3, G2);
  and and_9 (and_9_out, P4, P3, P2, G1);
  and and_10 (and_10_out, P4, P3, P2, P1, Cin);
  and and_11 (P, P4, P3, P2, P1);
  and and_12 (and_12_out, P4, G3);
  and and_13 (and_13_out, P4, P3, G2);
  and and_14 (and_14_out, P4, P3, P2, G1);
  or or_1 (C1, G1, and_1_out);
  or or_2 (C2, G2, and_2_out, and_3_out);
  or or_3 (C3, G3, and_4_out, and_5_out, and_6_out);
  or or_4 (C4, G4, and_7_out, and_8_out, and_9_out, and_10_out);
  or or_5 (G, G4, and_12_out, and_13_out, and_14_out);
endmodule

module \_4位并行加法器验证电路  (
  input  [3:0] X,
  input  [3:0] Y,
  input  C0,
  output [3:0] S,
  output C4,
  output C3
);

  wire and_1_out, and_2_out, and_3_out, and_4_out, and_5_out, and_6_out, and_7_out, and_8_out, or_3_out,
       or_4_out, xor_2_out, xor_3_out, xor_5_out, xor_8_out;

  or or_1 (C4, and_1_out, and_2_out);
  and and_1 (and_1_out, C3, xor_2_out);
  and and_2 (and_2_out, X[3], Y[3]);
  xor xor_1 (S[3], C3, xor_2_out);
  or or_2 (C3, and_3_out, and_4_out);
  xor xor_2 (xor_2_out, Y[3], X[3]);
  and and_3 (and_3_out, or_3_out, xor_3_out);
  xor xor_3 (xor_3_out, Y[2], X[2]);
  and and_4 (and_4_out, X[2], Y[2]);
  xor xor_4 (S[2], or_3_out, xor_3_out);
  or or_3 (or_3_out, and_6_out, and_5_out);
  and and_5 (and_5_out, X[1], Y[1]);
  and and_6 (and_6_out, or_4_out, xor_5_out);
  xor xor_5 (xor_5_out, Y[1], X[1]);
  xor xor_6 (S[1], or_4_out, xor_5_out);
  and and_7 (and_7_out, C0, xor_8_out);
  or or_4 (or_4_out, and_7_out, and_8_out);
  and and_8 (and_8_out, X[0], Y[0]);
  // Probe on X
  // Probe on Y
  // Probe on S
  xor xor_7 (S[0], xor_8_out, C0);
  xor xor_8 (xor_8_out, Y[0], X[0]);
  // Probe on X
  // Probe on Y
  // Probe on S

  // Notes on the sheet:
  //   C0: pull=down
  //   X: pull=down
  //   Y: pull=down
  //   输入引脚区
  //   4位快速加法器门电路版
  //   输出引脚区
  //   功能说明:4位Adder  S=X+Y，C4、C3分别为最高位、次高位进位位，C0为进位输入
  //   +
  //   =
  //   有符号加法
  //   +
  //   =
  //   无符号加法
endmodule

module \_8位加减法器验证电路  (
  input  [7:0] A,
  input  [7:0] B,
  input  Sub,
  input  Cin,
  output [7:0] S,
  output Cout,
  output Overflow,
  output SG
);

  wire \n4位并行加法器验证电路_1_c3 , \n4位并行加法器验证电路_2_c4 , xor_10_out;
  wire [3:0] xor_4_out, xor_9_out;

  xor xor_1 (xor_4_out[3], B[7], Sub);
  xor xor_2 (xor_4_out[2], B[6], Sub);
  xor xor_3 (xor_4_out[1], B[5], Sub);
  xor xor_4 (xor_4_out[0], B[4], Sub);
  \_4位并行加法器验证电路  \u_4位并行加法器验证电路_1  (
    .X(xor_4_out), .Y(A[7:4]), .C0(\n4位并行加法器验证电路_2_c4 ), .S(S[7:4]), .C4(Cout), .C3(\n4位并行加法器验证电路_1_c3 ));
  and and_1 (SG, S[7], 1'b1);
  xor xor_5 (xor_9_out[3], B[3], Sub);
  xor xor_6 (Overflow, Cout, \n4位并行加法器验证电路_1_c3 );
  xor xor_7 (xor_9_out[2], B[2], Sub);
  // Probe on A
  // Probe on B
  // Probe on Cin
  // Probe on S
  xor xor_8 (xor_9_out[1], B[1], Sub);
  xor xor_9 (xor_9_out[0], B[0], Sub);
  // Probe on A
  // Probe on B
  // Probe on Cin
  // Probe on S
  \_4位并行加法器验证电路  \u_4位并行加法器验证电路_2  (
    .X(xor_9_out), .Y(A[3:0]), .C0(xor_10_out), .S(S[3:0]), .C4(\n4位并行加法器验证电路_2_c4 ));  // open: C3
  xor xor_10 (xor_10_out, Sub, Cin);

  // Other names for the same wires on the sheet: A0_A3[3:0] = A[3:0]; A4_A7[3:0] = A[7:4]; B0_B3[3:0] = B[3:0];
  //   B4_B7[3:0] = B[7:4]; OF = Overflow

  // Notes on the sheet:
  //   S: pull=down
  //   A: pull=down
  //   Sub: pull=down
  //   Overflow: pull=down
  //   B: pull=down
  //   Cin: pull=down
  //   Cout: pull=down
  //   输入引脚区
  //   Cout为最高位进位位，Overflow为有符号溢出标志
  //   输出引脚区
  //   功能说明：8位可控加减法器    Sub=0 Cin=0: S=A+B；Sub=0 Cin=1: S=A+B+1；Sub=1 Cin=0: S=A-B；Sub=1 Cin=1: S=A-B-1。
  //   =
  //   有符号
  //   =
  //   无符号
endmodule

module _8bit_logic_operator (
  input  [7:0] A,
  input  [7:0] B,
  input  [1:0] Select,
  output [7:0] Y
);

  wire [7:0] and_1_out, not_1_out, or_1_out, xor_1_out;

  assign not_1_out = ~A;  // NOT_Gate not_1, 8 bits wide
  assign and_1_out = A & B;  // AND_Gate and_1, 8 bits wide
  assign or_1_out = A | B;  // OR_Gate or_1, 8 bits wide
  assign xor_1_out = A ^ B;  // XOR_Gate xor_1, 8 bits wide
  Multiplexer #(.select(2), .width(8)) multiplexer_1 (
    .in0(and_1_out), .in1(or_1_out), .in2(not_1_out), .in3(xor_1_out), .out(Y), .sel(Select));  // open: en
endmodule

module _8bit_shifter (
  input  [7:0] B,
  input  [2:0] N,
  input  [1:0] Select,
  output SOL,
  output [7:0] Y
);

  wire [7:0] shifter_1_out, shifter_2_out, shifter_3_out;

  Shifter shifter_1 (.in(B), .\dist (N), .out(shifter_1_out));
  Shifter #(.shift("lr")) shifter_2 (.in(B), .\dist (N), .out(shifter_2_out));
  Shifter #(.shift("ar")) shifter_3 (.in(B), .\dist (N), .out(shifter_3_out));
  Multiplexer #(.select(2), .width(8)) multiplexer_1 (
    .in0(B), .in1(shifter_1_out), .in2(shifter_2_out), .in3(shifter_3_out), .out(Y), .sel(Select));  // open: en

  assign SOL = B[7];
endmodule

module ALU (
  input  [2:0] N,
  input  [7:0] A,
  input  [7:0] B,
  input  [1:0] S,
  input  Cin,
  input  S2,
  input  S3,
  output A_B,
  output A__B,
  output A_B_2,
  output [7:0] Y,
  output OV,
  output SG,
  output CA,
  output ZO
);

  wire n8bit_shifter_1_sol, \n8位加减法器验证电路_1_cout ;
  wire [7:0] multiplexer_1_out, n8bit_logic_operator_1_y, n8bit_shifter_1_y, \n8位加减法器验证电路_1_s ;

  // Probe on A
  // Probe on B
  // Probe on N
  _8bit_shifter u_8bit_shifter_1 (.B(B), .N(N), .Select(S), .SOL(n8bit_shifter_1_sol), .Y(n8bit_shifter_1_y));
  \_8位加减法器验证电路  \u_8位加减法器验证电路_1  (
    .A(A), .B(B), .Sub(S[0]), .Cin(Cin), .S(\n8位加减法器验证电路_1_s ), .Cout(\n8位加减法器验证电路_1_cout ), .Overflow(OV),
    .SG(SG));
  _8bit_logic_operator u_8bit_logic_operator_1 (.A(A), .B(B), .Select(S), .Y(n8bit_logic_operator_1_y));
  Multiplexer #(.width(8), .enable("false")) multiplexer_1 (
    .in0(\n8位加减法器验证电路_1_s ), .in1(n8bit_logic_operator_1_y), .out(multiplexer_1_out), .sel(S2));
  Multiplexer #(.width(8), .enable("false")) multiplexer_2 (
    .in0(n8bit_shifter_1_y), .in1(multiplexer_1_out), .out(Y), .sel(S3));
  // Probe on Y
  Multiplexer #(.enable("false")) multiplexer_3 (
    .in0(n8bit_shifter_1_sol), .in1(\n8位加减法器验证电路_1_cout ), .out(CA), .sel(S3));
  Comparator comparator_1 (.a(A), .b(B), .gt(A_B), .eq(A__B), .lt(A_B_2));
  nor nor_1 (ZO, multiplexer_1_out[0], multiplexer_1_out[1], multiplexer_1_out[2], multiplexer_1_out[3], multiplexer_1_out[4], multiplexer_1_out[5], multiplexer_1_out[6], multiplexer_1_out[7]);

  // Notes on the sheet:
  //   OV: pull=down
  //   ZO: pull=down
  //   SG: pull=down
endmodule
