// Logisim project exp7.circ as structural Verilog: 15 circuits, main circuit EncodedCirc
module EncodedCirc (
  input  a,
  input  b,
  input  c,
  input  d,
  input  e,
  output x,
  output y,
  output z,
  output u
);

  wire and_2_out, and_3_out;

  and and_1 (x, a, c);
  and and_2 (and_2_out, a, b);
  and and_3 (and_3_out, a, d);
  or or_1 (u, e, c, a);
  or or_2 (y, e, d, and_2_out);
  or or_3 (z, c, b, and_3_out);
endmodule

module LEDCounter (
);

  wire button_1_out, button_2_out, button_3_out, button_4_out, button_5_out, encodedcirc_1_u,
       encodedcirc_1_x, encodedcirc_1_y, encodedcirc_1_z, main_1_out_6, main_1_out_7, main_1_out_8,
       main_1_out_9, main_1_out_10, n7_segment_disp_driver_1_a, n7_segment_disp_driver_1_b,
       n7_segment_disp_driver_1_c, n7_segment_disp_driver_1_d, n7_segment_disp_driver_1_e,
       n7_segment_disp_driver_1_f, n7_segment_disp_driver_1_g;

  Button button_1 (.out(button_1_out));
  Button button_2 (.out(button_2_out));
  Button button_3 (.out(button_3_out));
  Button button_4 (.out(button_4_out));
  Button button_5 (.out(button_5_out));
  EncodedCirc encodedcirc_1 (
    .a(button_1_out), .b(button_2_out), .c(button_3_out), .d(button_4_out), .e(button_5_out),
    .x(encodedcirc_1_x), .y(encodedcirc_1_y), .z(encodedcirc_1_z), .u(encodedcirc_1_u));
  LEDCounter_main main_1 (
    .in_1(button_1_out), .in_2(button_2_out), .in_3(button_3_out), .in_4(button_4_out), .in_5(button_5_out),
    .out_6(main_1_out_6), .out_7(main_1_out_7), .out_8(main_1_out_8), .out_9(main_1_out_9),
    .out_10(main_1_out_10));
  LED led_1 (.in(main_1_out_6));
  LED led_2 (.in(main_1_out_7));
  LED led_3 (.in(main_1_out_8));
  LED led_4 (.in(main_1_out_9));
  LED led_5 (.in(main_1_out_10));
  _7_Segment_Disp_Driver u_7_segment_disp_driver_1 (
    .In1(encodedcirc_1_x), .In2(encodedcirc_1_y), .In3(encodedcirc_1_z), .g(n7_segment_disp_driver_1_g),
    .In4(encodedcirc_1_u), .f(n7_segment_disp_driver_1_f), .a(n7_segment_disp_driver_1_a),
    .b(n7_segment_disp_driver_1_b), .e(n7_segment_disp_driver_1_e), .d(n7_segment_disp_driver_1_d),
    .c(n7_segment_disp_driver_1_c));
  _7_Segment_Display u_7_segment_display_1 (
    .g(n7_segment_disp_driver_1_g), .f(n7_segment_disp_driver_1_f), .a(n7_segment_disp_driver_1_a),
    .b(n7_segment_disp_driver_1_b), .e(n7_segment_disp_driver_1_e), .d(n7_segment_disp_driver_1_d),
    .c(n7_segment_disp_driver_1_c), .dp(1'b1));
endmodule

module Displayer_Keyboard (
);

  wire button_1_out, clock_1_out, clock_2_out, driverextendeddisp_1_a, driverextendeddisp_1_b,
       driverextendeddisp_1_c, driverextendeddisp_1_d, driverextendeddisp_1_e, driverextendeddisp_1_f,
       driverextendeddisp_1_g, keyboard_1_avail;
  wire [3:0] counter_1_q;
  wire [6:0] keyboard_1_data;
  wire [7:0] bit_extender_1_out, rom_1_data;

  Counter #(.width(4), .max('hf)) counter_1 (.Q(counter_1_q), .clk(clock_1_out));  // open: load, D, count, carry, clr
  Clock clock_1 (.out(clock_1_out));
  Clock clock_2 (.out(clock_2_out));
  Button button_1 (.out(button_1_out));
  DriverExtendedDisp driverextendeddisp_1 (
    .In1(counter_1_q[3]), .In2(counter_1_q[2]), .In3(counter_1_q[1]), .In4(counter_1_q[0]),
    .g(driverextendeddisp_1_g), .f(driverextendeddisp_1_f), .a(driverextendeddisp_1_a),
    .b(driverextendeddisp_1_b), .e(driverextendeddisp_1_e), .d(driverextendeddisp_1_d),
    .c(driverextendeddisp_1_c));
  _7_Segment_Display u_7_segment_display_1 (
    .g(driverextendeddisp_1_g), .f(driverextendeddisp_1_f), .a(driverextendeddisp_1_a),
    .b(driverextendeddisp_1_b), .e(driverextendeddisp_1_e), .d(driverextendeddisp_1_d),
    .c(driverextendeddisp_1_c), .dp(1'b1));
  assign bit_extender_1_out = {{4{1'b0}}, counter_1_q};  // Bit_Extender bit_extender_1
  Keyboard keyboard_1 (
    .clk(clock_2_out), .re(1'b1), .clr(button_1_out), .avail(keyboard_1_avail), .data(keyboard_1_data));
  ROM rom_1 (.addr(bit_extender_1_out), .data(rom_1_data));  // open: sel
  TTY tty_1 (.data(rom_1_data[6:0]), .clk(clock_1_out));  // open: we, clr
  TTY tty_2 (.data(keyboard_1_data), .clk(clock_2_out), .we(keyboard_1_avail), .clr(button_1_out));

  // Notes on the sheet:
  //   contents of rom_1 (hex, n*v repeats v):
  //   48 65 6c 6c 6f 57 6f 72 6c 64 21 32 30 32 34
endmodule

module DriverExtendedDisp (
  input  In1,
  input  In2,
  input  In3,
  input  In4,
  output g,
  output f,
  output a,
  output b,
  output e,
  output d,
  output c
);

  wire and_1_out, and_2_out, and_3_out, and_4_out, and_5_out, and_6_out, and_7_out, and_8_out, and_9_out,
       and_10_out, and_11_out, and_12_out, and_13_out, and_14_out, and_15_out, and_16_out, and_17_out,
       and_18_out, and_19_out, and_20_out, and_21_out, and_22_out, and_23_out, and_24_out, and_25_out,
       and_26_out, and_27_out, and_28_out, and_29_out, and_30_out, and_31_out, and_32_out, and_33_out,
       and_34_out, and_35_out, not_1_out, not_2_out, not_3_out, not_4_out, not_5_out, not_6_out, not_7_out,
       not_8_out, not_9_out, not_10_out, not_11_out, not_12_out, not_13_out, not_14_out, not_15_out,
       not_16_out, not_17_out, not_18_out, not_19_out, not_20_out, not_21_out, not_22_out, not_23_out,
       not_24_out, not_25_out, not_26_out, not_27_out, not_28_out, not_29_out, not_30_out, not_31_out,
       not_32_out, not_33_out, not_34_out, not_35_out, not_36_out, not_37_out, not_38_out, not_39_out,
       not_40_out, not_41_out, not_42_out, not_43_out;

  not not_1 (not_1_out, In2);
  and and_1 (and_1_out, not_1_out, In3);
  and and_2 (and_2_out, In3, not_2_out);
  not not_2 (not_2_out, In4);
  not not_3 (not_3_out, In1);
  and and_3 (and_3_out, not_3_out, In2, not_4_out);
  not not_4 (not_4_out, In3);
  and and_4 (and_4_out, In1, not_5_out);
  not not_5 (not_5_out, In2);
  and and_5 (and_5_out, In1, In4);
  not not_6 (not_6_out, In3);
  and and_6 (and_6_out, not_6_out, not_7_out);
  not not_7 (not_7_out, In4);
  not not_8 (not_8_out, In1);
  and and_7 (and_7_out, not_8_out, In2, not_9_out);
  not not_9 (not_9_out, In3);
  and and_8 (and_8_out, In2, not_10_out);
  not not_10 (not_10_out, In4);
  and and_9 (and_9_out, In1, not_11_out);
  not not_11 (not_11_out, In2);
  and and_10 (and_10_out, In1, In3);
  not not_12 (not_12_out, In2);
  and and_11 (and_11_out, not_12_out, not_13_out);
  not not_13 (not_13_out, In4);
  not not_14 (not_14_out, In1);
  and and_12 (and_12_out, not_14_out, In3);
  not not_15 (not_15_out, In1);
  and and_13 (and_13_out, not_15_out, In2, In4);
  and and_14 (and_14_out, In2, In3);
  and and_15 (and_15_out, In1, not_16_out, not_17_out);
  not not_16 (not_16_out, In2);
  not not_17 (not_17_out, In3);
  and and_16 (and_16_out, In1, not_18_out);
  not not_18 (not_18_out, In4);
  not not_19 (not_19_out, In1);
  and and_17 (and_17_out, not_19_out, not_20_out);
  not not_20 (not_20_out, In2);
  not not_21 (not_21_out, In1);
  not not_22 (not_22_out, In3);
  and and_18 (and_18_out, not_21_out, not_22_out, not_23_out);
  not not_23 (not_23_out, In4);
  not not_24 (not_24_out, In2);
  and and_19 (and_19_out, not_24_out, not_25_out);
  not not_25 (not_25_out, In4);
  not not_26 (not_26_out, In1);
  and and_20 (and_20_out, not_26_out, In3, In4);
  not not_27 (not_27_out, In3);
  and and_21 (and_21_out, In1, not_27_out, In4);
  not not_28 (not_28_out, In2);
  and and_22 (and_22_out, not_28_out, not_29_out);
  not not_29 (not_29_out, In4);
  and and_23 (and_23_out, In3, not_30_out);
  not not_30 (not_30_out, In4);
  and and_24 (and_24_out, In1, In3);
  and and_25 (and_25_out, In1, In2);
  not not_31 (not_31_out, In1);
  not not_32 (not_32_out, In2);
  and and_26 (and_26_out, not_31_out, not_32_out, not_33_out);
  not not_33 (not_33_out, In4);
  not not_34 (not_34_out, In2);
  and and_27 (and_27_out, not_34_out, In3, In4);
  not not_35 (not_35_out, In3);
  and and_28 (and_28_out, In2, not_35_out, In4);
  and and_29 (and_29_out, In2, In3, not_36_out);
  not not_36 (not_36_out, In4);
  and and_30 (and_30_out, In1, not_37_out);
  not not_37 (not_37_out, In3);
  not not_38 (not_38_out, In1);
  and and_31 (and_31_out, not_38_out, not_39_out);
  not not_39 (not_39_out, In3);
  not not_40 (not_40_out, In1);
  and and_32 (and_32_out, not_40_out, In4);
  not not_41 (not_41_out, In3);
  and and_33 (and_33_out, not_41_out, In4);
  not not_42 (not_42_out, In1);
  and and_34 (and_34_out, not_42_out, In2);
  and and_35 (and_35_out, In1, not_43_out);
  not not_43 (not_43_out, In2);
  or or_1 (g, and_1_out, and_2_out, and_3_out, and_4_out, and_5_out);
  or or_2 (f, and_6_out, and_7_out, and_8_out, and_9_out, and_10_out);
  or or_3 (b, and_17_out, and_18_out, and_19_out, and_20_out, and_21_out);
  or or_4 (e, and_22_out, and_23_out, and_24_out, and_25_out);
  or or_5 (d, and_26_out, and_27_out, and_28_out, and_29_out, and_30_out);
  or or_6 (c, and_31_out, and_32_out, and_33_out, and_34_out, and_35_out);
  or or_7 (a, and_11_out, and_12_out, and_13_out, and_14_out, and_15_out, and_16_out);
endmodule

module clock (
);

  wire clock_1_out, driverextendeddisp_1_a, driverextendeddisp_1_b, driverextendeddisp_1_c,
       driverextendeddisp_1_d, driverextendeddisp_1_e, driverextendeddisp_1_f, driverextendeddisp_1_g,
       driverextendeddisp_2_a, driverextendeddisp_2_b, driverextendeddisp_2_c, driverextendeddisp_2_d,
       driverextendeddisp_2_e, driverextendeddisp_2_f, driverextendeddisp_2_g, driverextendeddisp_3_a,
       driverextendeddisp_3_b, driverextendeddisp_3_c, driverextendeddisp_3_d, driverextendeddisp_3_e,
       driverextendeddisp_3_f, driverextendeddisp_3_g, driverextendeddisp_4_a, driverextendeddisp_4_b,
       driverextendeddisp_4_c, driverextendeddisp_4_d, driverextendeddisp_4_e, driverextendeddisp_4_f,
       driverextendeddisp_4_g, driverextendeddisp_5_a, driverextendeddisp_5_b, driverextendeddisp_5_c,
       driverextendeddisp_5_d, driverextendeddisp_5_e, driverextendeddisp_5_f, driverextendeddisp_5_g,
       driverextendeddisp_6_a, driverextendeddisp_6_b, driverextendeddisp_6_c, driverextendeddisp_6_d,
       driverextendeddisp_6_e, driverextendeddisp_6_f, driverextendeddisp_6_g, mod24_1_out_3, mod24_1_out_4,
       mod24_1_out_5, mod24_1_out_6, mod24_1_out_7, mod24_1_out_8, mod24_1_out_9, mod24_1_out_10,
       mod60_1_out_2, mod60_1_out_3, mod60_1_out_4, mod60_1_out_5, mod60_1_out_6, mod60_1_out_7,
       mod60_1_out_8, mod60_1_out_9, mod60_1_out_10, mod60_2_out_2, mod60_2_out_3, mod60_2_out_4,
       mod60_2_out_5, mod60_2_out_6, mod60_2_out_7, mod60_2_out_8, mod60_2_out_9, mod60_2_out_10;

  Mod24 mod24_1 (
    .CP(mod60_1_out_2), .out_3(mod24_1_out_3), .out_4(mod24_1_out_4), .out_5(mod24_1_out_5),
    .out_6(mod24_1_out_6), .out_7(mod24_1_out_7), .out_8(mod24_1_out_8), .out_9(mod24_1_out_9),
    .out_10(mod24_1_out_10));  // open: out_2
  DriverExtendedDisp driverextendeddisp_1 (
    .In1(mod24_1_out_3), .In2(mod24_1_out_4), .In3(mod24_1_out_5), .In4(mod24_1_out_6),
    .g(driverextendeddisp_1_g), .f(driverextendeddisp_1_f), .a(driverextendeddisp_1_a),
    .b(driverextendeddisp_1_b), .e(driverextendeddisp_1_e), .d(driverextendeddisp_1_d),
    .c(driverextendeddisp_1_c));
  _7_Segment_Display u_7_segment_display_1 (
    .g(driverextendeddisp_1_g), .f(driverextendeddisp_1_f), .a(driverextendeddisp_1_a),
    .b(driverextendeddisp_1_b), .e(driverextendeddisp_1_e), .d(driverextendeddisp_1_d),
    .c(driverextendeddisp_1_c), .dp(1'b1));
  DriverExtendedDisp driverextendeddisp_2 (
    .In1(mod24_1_out_7), .In2(mod24_1_out_8), .In3(mod24_1_out_9), .In4(mod24_1_out_10),
    .g(driverextendeddisp_2_g), .f(driverextendeddisp_2_f), .a(driverextendeddisp_2_a),
    .b(driverextendeddisp_2_b), .e(driverextendeddisp_2_e), .d(driverextendeddisp_2_d),
    .c(driverextendeddisp_2_c));
  Mod60 mod60_1 (
    .CP(mod60_2_out_2), .out_2(mod60_1_out_2), .out_3(mod60_1_out_3), .out_4(mod60_1_out_4),
    .out_5(mod60_1_out_5), .out_6(mod60_1_out_6), .out_7(mod60_1_out_7), .out_8(mod60_1_out_8),
    .out_9(mod60_1_out_9), .out_10(mod60_1_out_10));
  _7_Segment_Display u_7_segment_display_2 (
    .g(driverextendeddisp_2_g), .f(driverextendeddisp_2_f), .a(driverextendeddisp_2_a),
    .b(driverextendeddisp_2_b), .e(driverextendeddisp_2_e), .d(driverextendeddisp_2_d),
    .c(driverextendeddisp_2_c), .dp(1'b1));
  DriverExtendedDisp driverextendeddisp_3 (
    .In1(mod60_1_out_3), .In2(mod60_1_out_4), .In3(mod60_1_out_5), .In4(mod60_1_out_6),
    .g(driverextendeddisp_3_g), .f(driverextendeddisp_3_f), .a(driverextendeddisp_3_a),
    .b(driverextendeddisp_3_b), .e(driverextendeddisp_3_e), .d(driverextendeddisp_3_d),
    .c(driverextendeddisp_3_c));
  _7_Segment_Display u_7_segment_display_3 (
    .g(driverextendeddisp_3_g), .f(driverextendeddisp_3_f), .a(driverextendeddisp_3_a),
    .b(driverextendeddisp_3_b), .e(driverextendeddisp_3_e), .d(driverextendeddisp_3_d),
    .c(driverextendeddisp_3_c), .dp(1'b1));
  DriverExtendedDisp driverextendeddisp_4 (
    .In1(mod60_1_out_7), .In2(mod60_1_out_8), .In3(mod60_1_out_9), .In4(mod60_1_out_10),
    .g(driverextendeddisp_4_g), .f(driverextendeddisp_4_f), .a(driverextendeddisp_4_a),
    .b(driverextendeddisp_4_b), .e(driverextendeddisp_4_e), .d(driverextendeddisp_4_d),
    .c(driverextendeddisp_4_c));
  _7_Segment_Display u_7_segment_display_4 (
    .g(driverextendeddisp_4_g), .f(driverextendeddisp_4_f), .a(driverextendeddisp_4_a),
    .b(driverextendeddisp_4_b), .e(driverextendeddisp_4_e), .d(driverextendeddisp_4_d),
    .c(driverextendeddisp_4_c), .dp(1'b1));
  Clock clock_1 (.out(clock_1_out));
  Mod60 mod60_2 (
    .CP(clock_1_out), .out_2(mod60_2_out_2), .out_3(mod60_2_out_3), .out_4(mod60_2_out_4),
    .out_5(mod60_2_out_5), .out_6(mod60_2_out_6), .out_7(mod60_2_out_7), .out_8(mod60_2_out_8),
    .out_9(mod60_2_out_9), .out_10(mod60_2_out_10));
  DriverExtendedDisp driverextendeddisp_5 (
    .In1(mod60_2_out_3), .In2(mod60_2_out_4), .In3(mod60_2_out_5), .In4(mod60_2_out_6),
    .g(driverextendeddisp_5_g), .f(driverextendeddisp_5_f), .a(driverextendeddisp_5_a),
    .b(driverextendeddisp_5_b), .e(driverextendeddisp_5_e), .d(driverextendeddisp_5_d),
    .c(driverextendeddisp_5_c));
  DriverExtendedDisp driverextendeddisp_6 (
    .In1(mod60_2_out_7), .In2(mod60_2_out_8), .In3(mod60_2_out_9), .In4(mod60_2_out_10),
    .g(driverextendeddisp_6_g), .f(driverextendeddisp_6_f), .a(driverextendeddisp_6_a),
    .b(driverextendeddisp_6_b), .e(driverextendeddisp_6_e), .d(driverextendeddisp_6_d),
    .c(driverextendeddisp_6_c));
  _7_Segment_Display u_7_segment_display_5 (
    .g(driverextendeddisp_5_g), .f(driverextendeddisp_5_f), .a(driverextendeddisp_5_a),
    .b(driverextendeddisp_5_b), .e(driverextendeddisp_5_e), .d(driverextendeddisp_5_d),
    .c(driverextendeddisp_5_c), .dp(1'b1));
  _7_Segment_Display u_7_segment_display_6 (
    .g(driverextendeddisp_6_g), .f(driverextendeddisp_6_f), .a(driverextendeddisp_6_a),
    .b(driverextendeddisp_6_b), .e(driverextendeddisp_6_e), .d(driverextendeddisp_6_d),
    .c(driverextendeddisp_6_c), .dp(1'b1));
endmodule

module _74161N (
  input  \LD非 ,
  input  D0,
  input  D1,
  input  CP,
  input  D2,
  input  D3,
  input  \CR非 ,
  input  CTp,
  input  CTt,
  output Q0,
  output Q1,
  output Q2,
  output Q3,
  output CO
);

  wire and_1_out, and_2_out, and_3_out, and_4_out, and_5_out, and_6_out, and_7_out, and_8_out, and_9_out,
       and_10_out, and_11_out, and_12_out, nand_1_out, nand_2_out, nand_3_out, nand_4_out, nand_5_out,
       nand_6_out, nand_7_out, nand_8_out, not_1_out, not_2_out, or_1_out, or_2_out, or_3_out, or_4_out;

  not not_1 (not_1_out, \LD非 );
  not not_2 (not_2_out, \CR非 );
  and and_1 (and_1_out, CTp, CTt);
  and and_2 (and_2_out, Q0, and_1_out);
  and and_3 (and_3_out, Q1, Q0, and_1_out);
  and and_4 (and_4_out, Q2, Q1, Q0, and_1_out);
  nand nand_1 (nand_1_out, not_1_out, nand_2_out);
  nand nand_2 (nand_2_out, D0, not_1_out);
  nand nand_3 (nand_3_out, not_1_out, nand_4_out);
  nand nand_4 (nand_4_out, D1, not_1_out);
  nand nand_5 (nand_5_out, not_1_out, nand_6_out);
  nand nand_6 (nand_6_out, D2, not_1_out);
  nand nand_7 (nand_7_out, not_1_out, nand_8_out);
  nand nand_8 (nand_8_out, D3, not_1_out);
  or or_1 (or_1_out, and_1_out, not_1_out);
  or or_2 (or_2_out, and_2_out, not_1_out);
  or or_3 (or_3_out, and_3_out, not_1_out);
  or or_4 (or_4_out, and_4_out, not_1_out);
  and and_5 (and_5_out, nand_1_out, or_1_out);
  and and_6 (and_6_out, or_1_out, nand_2_out);
  and and_7 (and_7_out, nand_3_out, or_2_out);
  and and_8 (and_8_out, or_2_out, nand_4_out);
  and and_9 (and_9_out, nand_5_out, or_3_out);
  and and_10 (and_10_out, or_3_out, nand_6_out);
  and and_11 (and_11_out, nand_7_out, or_4_out);
  and and_12 (and_12_out, or_4_out, nand_8_out);
  J_K_Flip_Flop j_k_ff_1 (.J(and_5_out), .clk(CP), .K(and_6_out), .Q(Q0), .reset(not_2_out));  // open: Qn, preset, en
  J_K_Flip_Flop j_k_ff_2 (.J(and_7_out), .clk(CP), .K(and_8_out), .Q(Q1), .reset(not_2_out));  // open: Qn, preset, en
  J_K_Flip_Flop j_k_ff_3 (.J(and_9_out), .clk(CP), .K(and_10_out), .Q(Q2), .reset(not_2_out));  // open: Qn, preset, en
  J_K_Flip_Flop j_k_ff_4 (.J(and_11_out), .clk(CP), .K(and_12_out), .Q(Q3), .reset(not_2_out));  // open: Qn, preset, en
  and and_13 (CO, Q3, Q2, Q1, Q0, CTt);
endmodule

module Mod60 (
  input  CP,
  output out_2,
  output out_3,
  output out_4,
  output out_5,
  output out_6,
  output out_7,
  output out_8,
  output out_9,
  output out_10
);

  wire driverextendeddisp_1_a, driverextendeddisp_1_b, driverextendeddisp_1_c, driverextendeddisp_1_d,
       driverextendeddisp_1_e, driverextendeddisp_1_f, driverextendeddisp_1_g, driverextendeddisp_2_a,
       driverextendeddisp_2_b, driverextendeddisp_2_c, driverextendeddisp_2_d, driverextendeddisp_2_e,
       driverextendeddisp_2_f, driverextendeddisp_2_g, nand_1_out, nand_2_out;

  Clock clock_1 ();  // open: out
  and and_1 (out_2, out_4, out_6, out_7, out_10);
  _74161N u_74161n_1 (
    .\LD非 (nand_1_out), .D0(1'b0), .D1(1'b0), .CP(CP), .D2(1'b0), .D3(1'b0), .\CR非 (nand_2_out), .CTp(1'b1),
    .CTt(1'b1), .Q0(out_10), .Q1(out_9), .Q2(out_8), .Q3(out_7));  // open: CO
  DriverExtendedDisp driverextendeddisp_1 (
    .In1(out_7), .In2(out_8), .In3(out_9), .In4(out_10), .g(driverextendeddisp_1_g),
    .f(driverextendeddisp_1_f), .a(driverextendeddisp_1_a), .b(driverextendeddisp_1_b),
    .e(driverextendeddisp_1_e), .d(driverextendeddisp_1_d), .c(driverextendeddisp_1_c));
  nand nand_1 (nand_1_out, out_7, out_10);
  _7_Segment_Display u_7_segment_display_1 (
    .g(driverextendeddisp_1_g), .f(driverextendeddisp_1_f), .a(driverextendeddisp_1_a),
    .b(driverextendeddisp_1_b), .e(driverextendeddisp_1_e), .d(driverextendeddisp_1_d),
    .c(driverextendeddisp_1_c), .dp(1'b1));
  _74161N u_74161n_2 (
    .\LD非 (1'b1), .D0(1'b0), .D1(1'b0), .CP(nand_1_out), .D2(1'b0), .D3(1'b0), .\CR非 (nand_2_out),
    .CTp(1'b1), .CTt(1'b1), .Q0(out_6), .Q1(out_5), .Q2(out_4), .Q3(out_3));  // open: CO
  DriverExtendedDisp driverextendeddisp_2 (
    .In1(out_3), .In2(out_4), .In3(out_5), .In4(out_6), .g(driverextendeddisp_2_g),
    .f(driverextendeddisp_2_f), .a(driverextendeddisp_2_a), .b(driverextendeddisp_2_b),
    .e(driverextendeddisp_2_e), .d(driverextendeddisp_2_d), .c(driverextendeddisp_2_c));
  _7_Segment_Display u_7_segment_display_2 (
    .g(driverextendeddisp_2_g), .f(driverextendeddisp_2_f), .a(driverextendeddisp_2_a),
    .b(driverextendeddisp_2_b), .e(driverextendeddisp_2_e), .d(driverextendeddisp_2_d),
    .c(driverextendeddisp_2_c), .dp(1'b1));
  nand nand_2 (nand_2_out, out_5, out_4);

  // Other names for the same wires on the sheet: Q0_1 = out_10; Q0_2 = out_6; Q1_1 = out_9; Q1_2 = out_5;
  //   Q2_1 = out_8; Q2_2 = out_4; Q3_1 = out_7; Q3_2 = out_3; 进位 = out_2

  // Notes on the sheet:
  //   Low
  //   High
endmodule

module Mod24 (
  input  CP,
  output out_2,
  output out_3,
  output out_4,
  output out_5,
  output out_6,
  output out_7,
  output out_8,
  output out_9,
  output out_10
);

  wire driverextendeddisp_1_a, driverextendeddisp_1_b, driverextendeddisp_1_c, driverextendeddisp_1_d,
       driverextendeddisp_1_e, driverextendeddisp_1_f, driverextendeddisp_1_g, driverextendeddisp_2_a,
       driverextendeddisp_2_b, driverextendeddisp_2_c, driverextendeddisp_2_d, driverextendeddisp_2_e,
       driverextendeddisp_2_f, driverextendeddisp_2_g, nand_1_out, nand_2_out, nor_1_out, not_1_out;

  Clock clock_1 ();  // open: out
  and and_1 (out_2, out_5, out_9, out_10);
  _74161N u_74161n_1 (
    .\LD非 (nor_1_out), .D0(1'b0), .D1(1'b0), .CP(CP), .D2(1'b0), .D3(1'b0), .\CR非 (nand_2_out), .CTp(1'b1),
    .CTt(1'b1), .Q0(out_10), .Q1(out_9), .Q2(out_8), .Q3(out_7));  // open: CO
  DriverExtendedDisp driverextendeddisp_1 (
    .In1(out_7), .In2(out_8), .In3(out_9), .In4(out_10), .g(driverextendeddisp_1_g),
    .f(driverextendeddisp_1_f), .a(driverextendeddisp_1_a), .b(driverextendeddisp_1_b),
    .e(driverextendeddisp_1_e), .d(driverextendeddisp_1_d), .c(driverextendeddisp_1_c));
  nand nand_1 (nand_1_out, out_7, out_10);
  not not_1 (not_1_out, nand_1_out);
  nor nor_1 (nor_1_out, not_1_out, out_2);
  _7_Segment_Display u_7_segment_display_1 (
    .g(driverextendeddisp_1_g), .f(driverextendeddisp_1_f), .a(driverextendeddisp_1_a),
    .b(driverextendeddisp_1_b), .e(driverextendeddisp_1_e), .d(driverextendeddisp_1_d),
    .c(driverextendeddisp_1_c), .dp(1'b1));
  _74161N u_74161n_2 (
    .\LD非 (1'b1), .D0(1'b0), .D1(1'b0), .CP(nor_1_out), .D2(1'b0), .D3(1'b0), .\CR非 (nand_2_out), .CTp(1'b1),
    .CTt(1'b1), .Q0(out_6), .Q1(out_5), .Q2(out_4), .Q3(out_3));  // open: CO
  DriverExtendedDisp driverextendeddisp_2 (
    .In1(out_3), .In2(out_4), .In3(out_5), .In4(out_6), .g(driverextendeddisp_2_g),
    .f(driverextendeddisp_2_f), .a(driverextendeddisp_2_a), .b(driverextendeddisp_2_b),
    .e(driverextendeddisp_2_e), .d(driverextendeddisp_2_d), .c(driverextendeddisp_2_c));
  _7_Segment_Display u_7_segment_display_2 (
    .g(driverextendeddisp_2_g), .f(driverextendeddisp_2_f), .a(driverextendeddisp_2_a),
    .b(driverextendeddisp_2_b), .e(driverextendeddisp_2_e), .d(driverextendeddisp_2_d),
    .c(driverextendeddisp_2_c), .dp(1'b1));
  nand nand_2 (nand_2_out, out_5, out_6);

  // Other names for the same wires on the sheet: Q0_1 = out_10; Q0_2 = out_6; Q1_1 = out_9; Q1_2 = out_5;
  //   Q2_1 = out_8; Q2_2 = out_4; Q3_1 = out_7; Q3_2 = out_3; 进位 = out_2

  // Notes on the sheet:
  //   Low
  //   High
endmodule

module FibonacciDisp (
  input  in_1,
  input  \Reset_重启 
);

  wire and_1_out, clock_1_out, clock_2_out, comparator_1_lt, cu_1_p8, cu_1_p9, cu_1_p10, decoder_1_out0,
       decoder_1_out1, decoder_1_out2, decoder_1_out3, regs_1_p3;
  wire [1:0] counter_1_q, cu_1_p12, regs_1_p2, regs_1_p5, regs_1_p6;
  wire [3:0] multiplexer_1_out, subtractor_1_out;
  wire [4:0] cu_1_p11;
  wire [6:0] adder_1_out, bit_extender_2_out;
  wire [7:0] bit_extender_1_out, cu_1_p6, D, functionunit_1_p7, multiplexer_2_out, ram_1_data, register_1_q,
       regs_1_p7, regs_1_p8;
  wire [15:0] rom_1_data;

  Clock clock_1 (.out(clock_1_out));
  // Probe on register_1_q[3:0]
  // Probe on 4'b1010
  Register register_1 (.D(D), .en(and_1_out), .Q(register_1_q), .clk(clock_1_out));  // open: clr
  Clock clock_2 (.out(clock_2_out));
  // Probe on cu_1_p6
  Comparator #(.width(4), .mode("unsigned")) comparator_1 (
    .a(register_1_q[3:0]), .b(4'b1010), .lt(comparator_1_lt));  // open: gt, eq
  Decoder #(.select(2), .enable("false")) decoder_1 (
    .out0(decoder_1_out0), .out1(decoder_1_out1), .out2(decoder_1_out2), .out3(decoder_1_out3),
    .sel(counter_1_q));
  Counter #(.width(2), .max('h3)) counter_1 (
    .Q(counter_1_q), .clk(clock_2_out), .clr(\Reset_重启 ));  // open: load, D, count, carry
  ROM #(.dataWidth(16)) rom_1 (.addr(cu_1_p6), .data(rom_1_data), .sel(1'b1));
  // Probe on rom_1_data
  // Probe on D
  // Probe on D
  Subtractor #(.width(4)) subtractor_1 (.a(register_1_q[3:0]), .b(4'b1010), .out(subtractor_1_out));  // open: bin, bout
  // Regs regs_1: pin names not known; wires that end beside it: D, regs_1_p2, regs_1_p3, decoder_1_out3, regs_1_p5, regs_1_p6, regs_1_p7, regs_1_p8
  // Probe on multiplexer_1_out
  Multiplexer #(.width(4), .enable("false")) multiplexer_1 (
    .in0(subtractor_1_out), .in1(register_1_q[3:0]), .out(multiplexer_1_out), .sel(comparator_1_lt));
  // Probe on regs_1_p7
  // Probe on multiplexer_2_out
  // Probe on regs_1_p7
  // Probe on multiplexer_2_out
  assign bit_extender_1_out = {{4{1'b0}}, {regs_1_p6, cu_1_p12}};  // Bit_Extender bit_extender_1
  // CU cu_1: pin names not known; wires that end beside it: \Reset_重启 , decoder_1_out0, rom_1_data, decoder_1_out1, decoder_1_out3, cu_1_p6, regs_1_p3, cu_1_p8, cu_1_p9, cu_1_p10, cu_1_p11, {regs_1_p2, regs_1_p5, regs_1_p6, cu_1_p12}
  // Probe on {regs_1_p2, regs_1_p5, regs_1_p6, cu_1_p12}
  assign bit_extender_2_out = {{3{1'b0}}, multiplexer_1_out};  // Bit_Extender bit_extender_2
  Multiplexer #(.width(8), .enable("false")) multiplexer_2 (
    .in0(regs_1_p8), .in1(bit_extender_1_out), .out(multiplexer_2_out), .sel(cu_1_p8));
  // Probe on bit_extender_2_out
  RAM #(.bus("separate")) ram_1 (
    .addr(regs_1_p7), .din(multiplexer_2_out), .data(ram_1_data), .str(cu_1_p10), .sel(1'b1),
    .clk(decoder_1_out2), .ld(1'b1), .clr(in_1));
  // FunctionUnit functionunit_1: pin names not known; wires that end beside it: regs_1_p7, multiplexer_2_out, cu_1_p11[0], cu_1_p11[2:1], cu_1_p11[3], cu_1_p11[4], functionunit_1_p7
  Adder #(.width(7)) adder_1 (.a(bit_extender_2_out), .b(7'b0110000), .out(adder_1_out));  // open: cin, cout
  and and_1 (and_1_out, decoder_1_out2, cu_1_p10);
  Multiplexer #(.width(8), .enable("false")) multiplexer_3 (
    .in0(functionunit_1_p7), .in1(ram_1_data), .out(D), .sel(cu_1_p9));
  TTY #(.cols(16)) tty_1 (.data(adder_1_out), .clk(clock_1_out), .we(and_1_out));  // open: clr

  // Notes on the sheet:
  //   contents of rom_1 (hex, n*v repeats v):
  //   2001 2041 20c0 1084 4038 15f0 4 48 80fb
endmodule

module Parity_Check (
  input  [7:0] in_1,
  output False,
  output [7:0] out_3,
  output True
);

  wire after, \before , clock_1_out, comparator_1_gt, comparator_1_lt, odd_parity_1_out, odd_parity_2_out;
  wire [7:0] random_1_out;

  Comparator #(.width(1)) comparator_1 (.a(\before ), .b(after), .gt(comparator_1_gt), .eq(True), .lt(comparator_1_lt));
  or or_1 (False, comparator_1_gt, comparator_1_lt);
  xor odd_parity_1 (odd_parity_1_out, in_1[0], in_1[1], in_1[2], in_1[3], in_1[4], in_1[5], in_1[6], in_1[7]);
  // Probe on {\before , in_1}
  Multiplexer multiplexer_1 (.in0(1'b1), .in1(1'b0), .out(\before ), .sel(odd_parity_1_out));  // open: en
  // Probe on in_1
  Clock clock_1 (.out(clock_1_out));
  Adder adder_1 (.a(in_1), .b(random_1_out), .out(out_3));  // open: cin, cout
  Random random_1 (.clk(clock_1_out), .out(random_1_out));  // open: next, clr
  // Probe on out_3
  xor odd_parity_2 (odd_parity_2_out, out_3[0], out_3[1], out_3[2], out_3[3], out_3[4], out_3[5], out_3[6], out_3[7]);
  Multiplexer multiplexer_2 (.in0(1'b1), .in1(1'b0), .out(after), .sel(odd_parity_2_out));  // open: en
  // Probe on after

  // Other names for the same wires on the sheet: num[7:0] = out_3

  // Notes on the sheet:
  //   Encoder
  //   Random noise
  //   Decoder
endmodule

module _9bit_random_noise (
  input  CLK,
  input  [8:0] \_9位输入 ,
  output [8:0] \随机加扰屏蔽字 ,
  output [8:0] \加扰后数据 
);

  wire [4:0] \随机数_2_out , \随机数_3_out , \随机数_out ;
  wire [8:0] or_1_out;
  wire [31:0] decoder_1_out31, decoder_2_out31, decoder_3_out31;

  Decoder #(.select(5), .enable("false")) decoder_1 (
    .out0(decoder_1_out31[31]), .out1(decoder_1_out31[30]), .out2(decoder_1_out31[29]),
    .out3(decoder_1_out31[28]), .out4(decoder_1_out31[27]), .out5(decoder_1_out31[26]),
    .out6(decoder_1_out31[25]), .out7(decoder_1_out31[24]), .out8(decoder_1_out31[23]),
    .out9(decoder_1_out31[22]), .out10(decoder_1_out31[21]), .out11(decoder_1_out31[20]),
    .out12(decoder_1_out31[19]), .out13(decoder_1_out31[18]), .out14(decoder_1_out31[17]),
    .out15(decoder_1_out31[16]), .out16(decoder_1_out31[15]), .out17(decoder_1_out31[14]),
    .out18(decoder_1_out31[13]), .out19(decoder_1_out31[12]), .out20(decoder_1_out31[11]),
    .out21(decoder_1_out31[10]), .out22(decoder_1_out31[9]), .out23(decoder_1_out31[8]),
    .out24(decoder_1_out31[7]), .out25(decoder_1_out31[6]), .out26(decoder_1_out31[5]),
    .out27(decoder_1_out31[4]), .out28(decoder_1_out31[3]), .out29(decoder_1_out31[2]),
    .out30(decoder_1_out31[1]), .out31(decoder_1_out31[0]), .sel(\随机数_out ));
  Random #(.width(5)) \u_随机数  (.clk(CLK), .out(\随机数_out ));  // open: next, clr
  Random #(.width(5), .seed(18)) \u_随机数_2  (.clk(CLK), .out(\随机数_2_out ));  // open: next, clr
  Decoder #(.select(5), .enable("false")) decoder_2 (
    .out0(decoder_2_out31[31]), .out1(decoder_2_out31[30]), .out2(decoder_2_out31[29]),
    .out3(decoder_2_out31[28]), .out4(decoder_2_out31[27]), .out5(decoder_2_out31[26]),
    .out6(decoder_2_out31[25]), .out7(decoder_2_out31[24]), .out8(decoder_2_out31[23]),
    .out9(decoder_2_out31[22]), .out10(decoder_2_out31[21]), .out11(decoder_2_out31[20]),
    .out12(decoder_2_out31[19]), .out13(decoder_2_out31[18]), .out14(decoder_2_out31[17]),
    .out15(decoder_2_out31[16]), .out16(decoder_2_out31[15]), .out17(decoder_2_out31[14]),
    .out18(decoder_2_out31[13]), .out19(decoder_2_out31[12]), .out20(decoder_2_out31[11]),
    .out21(decoder_2_out31[10]), .out22(decoder_2_out31[9]), .out23(decoder_2_out31[8]),
    .out24(decoder_2_out31[7]), .out25(decoder_2_out31[6]), .out26(decoder_2_out31[5]),
    .out27(decoder_2_out31[4]), .out28(decoder_2_out31[3]), .out29(decoder_2_out31[2]),
    .out30(decoder_2_out31[1]), .out31(decoder_2_out31[0]), .sel(\随机数_2_out ));
  Decoder #(.select(5), .enable("false")) decoder_3 (
    .out0(decoder_3_out31[31]), .out1(decoder_3_out31[30]), .out2(decoder_3_out31[29]),
    .out3(decoder_3_out31[28]), .out4(decoder_3_out31[27]), .out5(decoder_3_out31[26]),
    .out6(decoder_3_out31[25]), .out7(decoder_3_out31[24]), .out8(decoder_3_out31[23]),
    .out9(decoder_3_out31[22]), .out10(decoder_3_out31[21]), .out11(decoder_3_out31[20]),
    .out12(decoder_3_out31[19]), .out13(decoder_3_out31[18]), .out14(decoder_3_out31[17]),
    .out15(decoder_3_out31[16]), .out16(decoder_3_out31[15]), .out17(decoder_3_out31[14]),
    .out18(decoder_3_out31[13]), .out19(decoder_3_out31[12]), .out20(decoder_3_out31[11]),
    .out21(decoder_3_out31[10]), .out22(decoder_3_out31[9]), .out23(decoder_3_out31[8]),
    .out24(decoder_3_out31[7]), .out25(decoder_3_out31[6]), .out26(decoder_3_out31[5]),
    .out27(decoder_3_out31[4]), .out28(decoder_3_out31[3]), .out29(decoder_3_out31[2]),
    .out30(decoder_3_out31[1]), .out31(decoder_3_out31[0]), .sel(\随机数_3_out ));
  Random #(.width(5), .seed(3)) \u_随机数_3  (.clk(CLK), .out(\随机数_3_out ));  // open: next, clr
  assign or_1_out = decoder_1_out31[8:0] | decoder_2_out31[8:0];  // OR_Gate or_1, 9 bits wide
  assign \随机加扰屏蔽字  = or_1_out | decoder_3_out31[8:0];  // OR_Gate or_2, 9 bits wide
  assign \加扰后数据  = \随机加扰屏蔽字  ^ \_9位输入 ;  // XOR_Gate xor_1, 9 bits wide
endmodule

module CRCencodder (
  input  [15:0] \原始数据 ,
  output [21:0] \CRC校验码 
);

  wire [4:0] multiplexer_1_out, multiplexer_2_out, multiplexer_3_out, multiplexer_4_out, multiplexer_5_out,
       multiplexer_6_out, multiplexer_7_out, multiplexer_8_out, multiplexer_9_out, multiplexer_10_out,
       multiplexer_11_out, multiplexer_12_out, multiplexer_13_out, multiplexer_14_out, multiplexer_15_out,
       multiplexer_16_out;

  Multiplexer #(.width(5), .enable("false")) multiplexer_1 (
    .in0({5{1'b0}}), .in1(5'b01010), .out(multiplexer_1_out), .sel(\原始数据 [0]));
  Multiplexer #(.width(5), .enable("false")) multiplexer_2 (
    .in0({5{1'b0}}), .in1(5'b10100), .out(multiplexer_2_out), .sel(\原始数据 [1]));
  Multiplexer #(.width(5), .enable("false")) multiplexer_3 (
    .in0({5{1'b0}}), .in1(5'b01101), .out(multiplexer_3_out), .sel(\原始数据 [2]));
  Multiplexer #(.width(5), .enable("false")) multiplexer_4 (
    .in0({5{1'b0}}), .in1(5'b11010), .out(multiplexer_4_out), .sel(\原始数据 [3]));
  Multiplexer #(.width(5), .enable("false")) multiplexer_5 (
    .in0({5{1'b0}}), .in1(5'b10001), .out(multiplexer_5_out), .sel(\原始数据 [4]));
  Multiplexer #(.width(5), .enable("false")) multiplexer_6 (
    .in0({5{1'b0}}), .in1(5'b00111), .out(multiplexer_6_out), .sel(\原始数据 [5]));
  Multiplexer #(.width(5), .enable("false")) multiplexer_7 (
    .in0({5{1'b0}}), .in1(5'b01110), .out(multiplexer_7_out), .sel(\原始数据 [6]));
  Multiplexer #(.width(5), .enable("false")) multiplexer_8 (
    .in0({5{1'b0}}), .in1(5'b11100), .out(multiplexer_8_out), .sel(\原始数据 [7]));
  Multiplexer #(.width(5), .enable("false")) multiplexer_9 (
    .in0({5{1'b0}}), .in1(5'b11101), .out(multiplexer_9_out), .sel(\原始数据 [8]));
  Multiplexer #(.width(5), .enable("false")) multiplexer_10 (
    .in0({5{1'b0}}), .in1({5{1'b1}}), .out(multiplexer_10_out), .sel(\原始数据 [9]));
  Multiplexer #(.width(5), .enable("false")) multiplexer_11 (
    .in0({5{1'b0}}), .in1(5'b11011), .out(multiplexer_11_out), .sel(\原始数据 [10]));
  Multiplexer #(.width(5), .enable("false")) multiplexer_12 (
    .in0({5{1'b0}}), .in1(5'b10011), .out(multiplexer_12_out), .sel(\原始数据 [11]));
  Multiplexer #(.width(5), .enable("false")) multiplexer_13 (
    .in0({5{1'b0}}), .in1(5'b00011), .out(multiplexer_13_out), .sel(\原始数据 [12]));
  Multiplexer #(.width(5), .enable("false")) multiplexer_14 (
    .in0({5{1'b0}}), .in1(5'b00110), .out(multiplexer_14_out), .sel(\原始数据 [13]));
  Multiplexer #(.width(5), .enable("false")) multiplexer_15 (
    .in0({5{1'b0}}), .in1(5'b01100), .out(multiplexer_15_out), .sel(\原始数据 [14]));
  Multiplexer #(.width(5), .enable("false")) multiplexer_16 (
    .in0({5{1'b0}}), .in1(5'b11000), .out(multiplexer_16_out), .sel(\原始数据 [15]));
  assign \CRC校验码 [4:0] = multiplexer_1_out ^ multiplexer_2_out ^ multiplexer_3_out ^ multiplexer_4_out ^ multiplexer_5_out ^ multiplexer_6_out ^ multiplexer_7_out ^ multiplexer_8_out ^ multiplexer_9_out ^ multiplexer_10_out ^ multiplexer_11_out ^ multiplexer_12_out ^ multiplexer_13_out ^ multiplexer_14_out ^ multiplexer_15_out ^ multiplexer_16_out;  // XOR_Gate xor_1, 5 bits wide
  xor xor_2 (\CRC校验码 [5], \原始数据 [15], \原始数据 [14], \原始数据 [13], \原始数据 [12], \原始数据 [11], \原始数据 [10], \原始数据 [9], \原始数据 [8], \原始数据 [7], \原始数据 [6], \原始数据 [5], \原始数据 [4], \原始数据 [3], \原始数据 [2], \原始数据 [1], \原始数据 [0], \CRC校验码 [0], \CRC校验码 [1], \CRC校验码 [2], \CRC校验码 [3], \CRC校验码 [4]);

  assign \CRC校验码 [21:6] = \原始数据 ;

  // Other names for the same wires on the sheet: CRC编码[21:0] = {\原始数据 , \CRC校验码 [5:0]}; r1 = \CRC校验码 [0];
  //   r2 = \CRC校验码 [1]; r3 = \CRC校验码 [2]; r4 = \CRC校验码 [3]; r5 = \CRC校验码 [4]; P = \CRC校验码 [5]; r6 = \CRC校验码 [5];
  //   D1 = \原始数据 [0]; Data[15:0] = \原始数据 ; D2 = \原始数据 [1]; D3 = \原始数据 [2]; D4 = \原始数据 [3]; D5 = \原始数据 [4];
  //   D6 = \原始数据 [5]; D7 = \原始数据 [6]; D8 = \原始数据 [7]; D9 = \原始数据 [8]; D10 = \原始数据 [9]; D11 = \原始数据 [10];
  //   D12 = \原始数据 [11]; D13 = \原始数据 [12]; D14 = \原始数据 [13]; D15 = \原始数据 [14]; D16 = \原始数据 [15]

  // Notes on the sheet:
  //   输出引脚区
endmodule

module CRCdecoder (
  input  [21:0] \CRC编码 ,
  output \_0位错 ,
  output \_1位错 ,
  output \_2位错 ,
  output [15:0] \纠错后数据 
);

  wire and_1_out, and_2_out, nor_1_out, nor_2_out, nor_3_out, nor_4_out, nor_5_out, nor_6_out, nor_7_out,
       nor_8_out, nor_9_out, nor_10_out, nor_11_out, nor_12_out, nor_13_out, nor_14_out, nor_15_out,
       nor_16_out, not_1_out, not_2_out, or_1_out, \总校验位错 ;
  wire [4:0] multiplexer_1_out, multiplexer_2_out, multiplexer_3_out, multiplexer_4_out, multiplexer_5_out,
       multiplexer_6_out, multiplexer_7_out, multiplexer_8_out, multiplexer_9_out, multiplexer_10_out,
       multiplexer_11_out, multiplexer_12_out, multiplexer_13_out, multiplexer_14_out, multiplexer_15_out,
       multiplexer_16_out, xor_2_out, xor_3_out, xor_4_out, xor_5_out, xor_6_out, xor_7_out, xor_8_out,
       xor_9_out, xor_10_out, xor_11_out, xor_12_out, xor_13_out, xor_14_out, xor_15_out, xor_16_out,
       xor_17_out, xor_18_out;

  xor xor_1 (\总校验位错 , \CRC编码 [21], \CRC编码 [20], \CRC编码 [19], \CRC编码 [18], \CRC编码 [17], \CRC编码 [16], \CRC编码 [15], \CRC编码 [14], \CRC编码 [13], \CRC编码 [12], \CRC编码 [11], \CRC编码 [10], \CRC编码 [9], \CRC编码 [8], \CRC编码 [7], \CRC编码 [6], \CRC编码 [5], \CRC编码 [4], \CRC编码 [3], \CRC编码 [2], \CRC编码 [1], \CRC编码 [0]);
  Multiplexer #(.width(5), .enable("false")) multiplexer_1 (
    .in0({5{1'b0}}), .in1(5'b01010), .out(multiplexer_1_out), .sel(\CRC编码 [6]));
  Multiplexer #(.width(5), .enable("false")) multiplexer_2 (
    .in0({5{1'b0}}), .in1(5'b10100), .out(multiplexer_2_out), .sel(\CRC编码 [7]));
  Multiplexer #(.width(5), .enable("false")) multiplexer_3 (
    .in0({5{1'b0}}), .in1(5'b01101), .out(multiplexer_3_out), .sel(\CRC编码 [8]));
  Multiplexer #(.width(5), .enable("false")) multiplexer_4 (
    .in0({5{1'b0}}), .in1(5'b11010), .out(multiplexer_4_out), .sel(\CRC编码 [9]));
  Multiplexer #(.width(5), .enable("false")) multiplexer_5 (
    .in0({5{1'b0}}), .in1(5'b10001), .out(multiplexer_5_out), .sel(\CRC编码 [10]));
  Multiplexer #(.width(5), .enable("false")) multiplexer_6 (
    .in0({5{1'b0}}), .in1(5'b00111), .out(multiplexer_6_out), .sel(\CRC编码 [11]));
  Multiplexer #(.width(5), .enable("false")) multiplexer_7 (
    .in0({5{1'b0}}), .in1(5'b01110), .out(multiplexer_7_out), .sel(\CRC编码 [12]));
  Multiplexer #(.width(5), .enable("false")) multiplexer_8 (
    .in0({5{1'b0}}), .in1(5'b11100), .out(multiplexer_8_out), .sel(\CRC编码 [13]));
  Multiplexer #(.width(5), .enable("false")) multiplexer_9 (
    .in0({5{1'b0}}), .in1(5'b11101), .out(multiplexer_9_out), .sel(\CRC编码 [14]));
  Multiplexer #(.width(5), .enable("false")) multiplexer_10 (
    .in0({5{1'b0}}), .in1({5{1'b1}}), .out(multiplexer_10_out), .sel(\CRC编码 [15]));
  Multiplexer #(.width(5), .enable("false")) multiplexer_11 (
    .in0({5{1'b0}}), .in1(5'b11011), .out(multiplexer_11_out), .sel(\CRC编码 [16]));
  Multiplexer #(.width(5), .enable("false")) multiplexer_12 (
    .in0({5{1'b0}}), .in1(5'b10011), .out(multiplexer_12_out), .sel(\CRC编码 [17]));
  Multiplexer #(.width(5), .enable("false")) multiplexer_13 (
    .in0({5{1'b0}}), .in1(5'b00011), .out(multiplexer_13_out), .sel(\CRC编码 [18]));
  Multiplexer #(.width(5), .enable("false")) multiplexer_14 (
    .in0({5{1'b0}}), .in1(5'b00110), .out(multiplexer_14_out), .sel(\CRC编码 [19]));
  Multiplexer #(.width(5), .enable("false")) multiplexer_15 (
    .in0({5{1'b0}}), .in1(5'b01100), .out(multiplexer_15_out), .sel(\CRC编码 [20]));
  Multiplexer #(.width(5), .enable("false")) multiplexer_16 (
    .in0({5{1'b0}}), .in1(5'b11000), .out(multiplexer_16_out), .sel(\CRC编码 [21]));
  assign xor_2_out = multiplexer_1_out ^ multiplexer_2_out ^ multiplexer_3_out ^ multiplexer_4_out ^ multiplexer_5_out ^ multiplexer_6_out ^ multiplexer_7_out ^ multiplexer_8_out ^ multiplexer_9_out ^ multiplexer_10_out ^ multiplexer_11_out ^ multiplexer_12_out ^ multiplexer_13_out ^ multiplexer_14_out ^ multiplexer_15_out ^ multiplexer_16_out ^ \CRC编码 [4:0];  // XOR_Gate xor_2, 5 bits wide
  or or_1 (or_1_out, xor_2_out[0], xor_2_out[1], xor_2_out[2], xor_2_out[3], xor_2_out[4]);
  assign xor_3_out = xor_2_out ^ 5'b01010;  // XOR_Gate xor_3, 5 bits wide
  assign xor_4_out = xor_2_out ^ 5'b10100;  // XOR_Gate xor_4, 5 bits wide
  assign xor_5_out = xor_2_out ^ 5'b01101;  // XOR_Gate xor_5, 5 bits wide
  assign xor_6_out = xor_2_out ^ 5'b11010;  // XOR_Gate xor_6, 5 bits wide
  assign xor_7_out = xor_2_out ^ 5'b10001;  // XOR_Gate xor_7, 5 bits wide
  assign xor_8_out = xor_2_out ^ 5'b00111;  // XOR_Gate xor_8, 5 bits wide
  assign xor_9_out = xor_2_out ^ 5'b01110;  // XOR_Gate xor_9, 5 bits wide
  assign xor_10_out = xor_2_out ^ 5'b11100;  // XOR_Gate xor_10, 5 bits wide
  assign xor_11_out = xor_2_out ^ 5'b11101;  // XOR_Gate xor_11, 5 bits wide
  assign xor_12_out = xor_2_out ^ {5{1'b1}};  // XOR_Gate xor_12, 5 bits wide
  assign xor_13_out = xor_2_out ^ 5'b11011;  // XOR_Gate xor_13, 5 bits wide
  assign xor_14_out = xor_2_out ^ 5'b10011;  // XOR_Gate xor_14, 5 bits wide
  assign xor_15_out = xor_2_out ^ 5'b00011;  // XOR_Gate xor_15, 5 bits wide
  assign xor_16_out = xor_2_out ^ 5'b00110;  // XOR_Gate xor_16, 5 bits wide
  assign xor_17_out = xor_2_out ^ 5'b01100;  // XOR_Gate xor_17, 5 bits wide
  assign xor_18_out = xor_2_out ^ 5'b11000;  // XOR_Gate xor_18, 5 bits wide
  and and_1 (and_1_out, \总校验位错 , or_1_out);
  not not_1 (not_1_out, or_1_out);
  not not_2 (not_2_out, \总校验位错 );
  not not_3 (\_0位错 , or_1_out);
  nor nor_1 (nor_1_out, xor_3_out[0], xor_3_out[1], xor_3_out[2], xor_3_out[3], xor_3_out[4]);
  nor nor_2 (nor_2_out, xor_4_out[0], xor_4_out[1], xor_4_out[2], xor_4_out[3], xor_4_out[4]);
  nor nor_3 (nor_3_out, xor_5_out[0], xor_5_out[1], xor_5_out[2], xor_5_out[3], xor_5_out[4]);
  nor nor_4 (nor_4_out, xor_6_out[0], xor_6_out[1], xor_6_out[2], xor_6_out[3], xor_6_out[4]);
  nor nor_5 (nor_5_out, xor_7_out[0], xor_7_out[1], xor_7_out[2], xor_7_out[3], xor_7_out[4]);
  nor nor_6 (nor_6_out, xor_8_out[0], xor_8_out[1], xor_8_out[2], xor_8_out[3], xor_8_out[4]);
  nor nor_7 (nor_7_out, xor_9_out[0], xor_9_out[1], xor_9_out[2], xor_9_out[3], xor_9_out[4]);
  nor nor_8 (nor_8_out, xor_10_out[0], xor_10_out[1], xor_10_out[2], xor_10_out[3], xor_10_out[4]);
  nor nor_9 (nor_9_out, xor_11_out[0], xor_11_out[1], xor_11_out[2], xor_11_out[3], xor_11_out[4]);
  nor nor_10 (nor_10_out, xor_12_out[0], xor_12_out[1], xor_12_out[2], xor_12_out[3], xor_12_out[4]);
  nor nor_11 (nor_11_out, xor_13_out[0], xor_13_out[1], xor_13_out[2], xor_13_out[3], xor_13_out[4]);
  nor nor_12 (nor_12_out, xor_14_out[0], xor_14_out[1], xor_14_out[2], xor_14_out[3], xor_14_out[4]);
  nor nor_13 (nor_13_out, xor_15_out[0], xor_15_out[1], xor_15_out[2], xor_15_out[3], xor_15_out[4]);
  nor nor_14 (nor_14_out, xor_16_out[0], xor_16_out[1], xor_16_out[2], xor_16_out[3], xor_16_out[4]);
  nor nor_15 (nor_15_out, xor_17_out[0], xor_17_out[1], xor_17_out[2], xor_17_out[3], xor_17_out[4]);
  nor nor_16 (nor_16_out, xor_18_out[0], xor_18_out[1], xor_18_out[2], xor_18_out[3], xor_18_out[4]);
  and and_2 (and_2_out, \总校验位错 , not_1_out);
  and and_3 (\_2位错 , not_2_out, or_1_out);
  xor xor_19 (\纠错后数据 [0], nor_1_out, \CRC编码 [6]);
  xor xor_20 (\纠错后数据 [1], nor_2_out, \CRC编码 [7]);
  xor xor_21 (\纠错后数据 [2], nor_3_out, \CRC编码 [8]);
  xor xor_22 (\纠错后数据 [3], nor_4_out, \CRC编码 [9]);
  xor xor_23 (\纠错后数据 [4], nor_5_out, \CRC编码 [10]);
  xor xor_24 (\纠错后数据 [5], nor_6_out, \CRC编码 [11]);
  xor xor_25 (\纠错后数据 [6], nor_7_out, \CRC编码 [12]);
  xor xor_26 (\纠错后数据 [7], nor_8_out, \CRC编码 [13]);
  xor xor_27 (\纠错后数据 [8], nor_9_out, \CRC编码 [14]);
  xor xor_28 (\纠错后数据 [9], nor_10_out, \CRC编码 [15]);
  xor xor_29 (\纠错后数据 [10], nor_11_out, \CRC编码 [16]);
  xor xor_30 (\纠错后数据 [11], nor_12_out, \CRC编码 [17]);
  xor xor_31 (\纠错后数据 [12], nor_13_out, \CRC编码 [18]);
  xor xor_32 (\纠错后数据 [13], nor_14_out, \CRC编码 [19]);
  xor xor_33 (\纠错后数据 [14], nor_15_out, \CRC编码 [20]);
  xor xor_34 (\纠错后数据 [15], nor_16_out, \CRC编码 [21]);
  or or_2 (\_1位错 , and_1_out, and_2_out);

  // Other names for the same wires on the sheet: CRC[21:0] = \CRC编码 ; r3 = \CRC编码 [2]; r4 = \CRC编码 [3];
  //   r5 = \CRC编码 [4]; r1 = \CRC编码 [0]; r2 = \CRC编码 [1]; r6 = \CRC编码 [5]; D1 = \CRC编码 [6]; D2 = \CRC编码 [7];
  //   D3 = \CRC编码 [8]; D4 = \CRC编码 [9]; D5 = \CRC编码 [10]; D6 = \CRC编码 [11]; D7 = \CRC编码 [12]; D8 = \CRC编码 [13];
  //   D9 = \CRC编码 [14]; D10 = \CRC编码 [15]; D11 = \CRC编码 [16]; D12 = \CRC编码 [17]; D13 = \CRC编码 [18]; D14 = \CRC编码 [19];
  //   D15 = \CRC编码 [20]; D16 = \CRC编码 [21]

  // Notes on the sheet:
  //   输入引脚区
  //   输出引脚区
endmodule

module CRCcheck (
  input  [15:0] \原始数据 ,
  input  [1:0] \加扰控制 
);

  wire clock_1_out, comparator_1_eq, \crcdecoder_1__0位错 , \crcdecoder_1__1位错 , \crcdecoder_1__2位错 ;
  wire [15:0] \crcdecoder_1_纠错后数据 ;
  wire [21:0] \crcencodder_1_crc校验码 , \n22bit_noise_1_加扰后数据 , \n22bit_noise_1_随机加扰屏蔽字 ;

  // Probe on \原始数据 
  CRCencodder crcencodder_1 (.\原始数据 (\原始数据 ), .\CRC校验码 (\crcencodder_1_crc校验码 ));
  // Probe on \crcencodder_1_crc校验码 
  // Probe on \crcencodder_1_crc校验码 
  // Probe on \n22bit_noise_1_随机加扰屏蔽字 
  Clock clock_1 (.out(clock_1_out));
  // Probe on \n22bit_noise_1_加扰后数据 
  _22bit_noise u_22bit_noise_1 (
    .CLK(clock_1_out), .\_22位输入 (\crcencodder_1_crc校验码 ), .\加扰模式 (\加扰控制 ),
    .\随机加扰屏蔽字 (\n22bit_noise_1_随机加扰屏蔽字 ), .\加扰后数据 (\n22bit_noise_1_加扰后数据 ));  // open: 增加三位错, EDU
  // Probe on \n22bit_noise_1_加扰后数据 
  LED \u_两位错  (.in(\crcdecoder_1__1位错 ));
  LED OK (.in(\crcdecoder_1__2位错 ));
  LED \u_一位错  (.in(\crcdecoder_1__0位错 ));
  CRCdecoder crcdecoder_1 (
    .\CRC编码 (\n22bit_noise_1_加扰后数据 ), .\_0位错 (\crcdecoder_1__0位错 ), .\_1位错 (\crcdecoder_1__1位错 ),
    .\_2位错 (\crcdecoder_1__2位错 ), .\纠错后数据 (\crcdecoder_1_纠错后数据 ));
  // Probe on \crcdecoder_1_纠错后数据 
  LED \u_数据正确  (.in(comparator_1_eq));
  Comparator #(.width(16)) comparator_1 (.a(\原始数据 ), .b(\crcdecoder_1_纠错后数据 ), .eq(comparator_1_eq));  // open: gt, lt

  // Notes on the sheet:
  //   CRC编码
  //   CRC解码
endmodule

module _22bit_noise (
  input  CLK,
  input  [21:0] \_22位输入 ,
  input  EDU,
  input  [1:0] \加扰模式 ,
  input  \增加三位错 ,
  output [21:0] \随机加扰屏蔽字 ,
  output [21:0] \加扰后数据 
);

  wire comparator_1_eq, \随机信号_5_out ;
  wire [1:0] EDUerr, multiplexer_3_out, \随机信号_4_out ;
  wire [3:0] \随机信号_2_out , \随机信号_3_out , \随机信号_out ;
  wire [7:0] counter_1_q;
  wire [15:0] \_1位加扰A ;
  wire [21:0] \_1位加扰 , \_2位加扰 , \_3位加扰 , multiplexer_1_out, multiplexer_5_out, shifter_1_out, \随机加扰 ;
  wire [21:6] \_1位加扰B , \_1位加扰C ;

  Decoder #(.select(4), .enable("false")) decoder_1 (
    .out0(\_1位加扰A [0]), .out1(\_1位加扰A [1]), .out2(\_1位加扰A [2]), .out3(\_1位加扰A [3]), .out4(\_1位加扰A [4]),
    .out5(\_1位加扰A [5]), .out6(\_1位加扰A [6]), .out7(\_1位加扰A [7]), .out8(\_1位加扰A [8]), .out9(\_1位加扰A [9]),
    .out10(\_1位加扰A [10]), .out11(\_1位加扰A [11]), .out12(\_1位加扰A [12]), .out13(\_1位加扰A [13]),
    .out14(\_1位加扰A [14]), .out15(\_1位加扰A [15]), .sel(\随机信号_out ));
  Random #(.width(4)) \u_随机信号  (.clk(CLK), .out(\随机信号_out ));  // open: next, clr
  Random #(.width(4), .seed(18)) \u_随机信号_2  (.clk(CLK), .out(\随机信号_2_out ));  // open: next, clr
  Decoder #(.select(4), .enable("false")) decoder_2 (
    .out0(\_1位加扰B [6]), .out1(\_1位加扰B [7]), .out2(\_1位加扰B [8]), .out3(\_1位加扰B [9]), .out4(\_1位加扰B [10]),
    .out5(\_1位加扰B [11]), .out6(\_1位加扰B [12]), .out7(\_1位加扰B [13]), .out8(\_1位加扰B [14]), .out9(\_1位加扰B [15]),
    .out10(\_1位加扰B [16]), .out11(\_1位加扰B [17]), .out12(\_1位加扰B [18]), .out13(\_1位加扰B [19]),
    .out14(\_1位加扰B [20]), .out15(\_1位加扰B [21]), .sel(\随机信号_2_out ));
  Random #(.width(4), .seed(3)) \u_随机信号_3  (.clk(CLK), .out(\随机信号_3_out ));  // open: next, clr
  Random #(.width(2), .seed(21)) \u_随机信号_4  (.clk(CLK), .out(\随机信号_4_out ));  // open: next, clr
  Random #(.width(1), .seed(31)) \u_随机信号_5  (.clk(CLK), .out(\随机信号_5_out ));  // open: next, clr
  Decoder #(.select(4), .enable("false")) decoder_3 (
    .out0(\_1位加扰C [6]), .out1(\_1位加扰C [7]), .out2(\_1位加扰C [8]), .out3(\_1位加扰C [9]), .out4(\_1位加扰C [10]),
    .out5(\_1位加扰C [11]), .out6(\_1位加扰C [12]), .out7(\_1位加扰C [13]), .out8(\_1位加扰C [14]), .out9(\_1位加扰C [15]),
    .out10(\_1位加扰C [16]), .out11(\_1位加扰C [17]), .out12(\_1位加扰C [18]), .out13(\_1位加扰C [19]),
    .out14(\_1位加扰C [20]), .out15(\_1位加扰C [21]), .sel(\随机信号_3_out ));
  Pull_Resistor #(.pull(1)) pull_resistor_1 (.node(\加扰模式 ));
  Pull_Resistor pull_resistor_2 (.node(\增加三位错 ));
  Multiplexer #(.width(22), .enable("false")) multiplexer_1 (
    .in0({\_1位加扰B , {6{1'b0}}}), .in1(\_3位加扰 ), .out(multiplexer_1_out), .sel(\增加三位错 ));
  Multiplexer #(.select(2), .width(22), .enable("false")) multiplexer_2 (
    .in0({22{1'b0}}), .in1({{6{1'b0}}, \_1位加扰A }), .in2(\_2位加扰 ), .in3(multiplexer_1_out), .out(\随机加扰 ),
    .sel(\随机信号_4_out ));
  Pull_Resistor pull_resistor_3 (.node(EDU));
  Multiplexer #(.width(2), .enable("false")) multiplexer_3 (
    .in0(\加扰模式 ), .in1(EDUerr), .out(multiplexer_3_out), .sel(EDU));
  Shifter #(.width(22), .shift("rl")) shifter_1 (.in({{6{1'b0}}, \_1位加扰A }), .\dist (5'b00001), .out(shifter_1_out));
  Comparator #(.width(22), .mode("unsigned")) comparator_1 (
    .a({{6{1'b0}}, \_1位加扰A }), .b({\_1位加扰B , {6{1'b0}}}), .eq(comparator_1_eq));  // open: gt, lt
  Multiplexer #(.select(2), .width(22), .enable("false")) multiplexer_4 (
    .in0({22{1'b0}}), .in1(\_1位加扰 ), .in2(\_2位加扰 ), .in3(\随机加扰 ), .out(\随机加扰屏蔽字 ), .sel(multiplexer_3_out));
  Multiplexer #(.width(22), .enable("false")) multiplexer_5 (
    .in0({{6{1'b0}}, \_1位加扰A }), .in1(shifter_1_out), .out(multiplexer_5_out), .sel(comparator_1_eq));
  Counter counter_1 (.Q(counter_1_q), .clk(CLK));  // open: load, D, count, carry, clr
  assign \_2位加扰  = multiplexer_5_out ^ {\_1位加扰B , {6{1'b0}}};  // XOR_Gate xor_1, 22 bits wide
  assign \_3位加扰  = \_2位加扰  ^ {\_1位加扰C , {6{1'b0}}};  // XOR_Gate xor_2, 22 bits wide
  ROM #(.dataWidth(2)) rom_1 (.addr(counter_1_q), .data(EDUerr));  // open: sel
  Multiplexer #(.width(22), .enable("false")) multiplexer_6 (
    .in0(multiplexer_5_out), .in1({\_1位加扰B , {6{1'b0}}}), .out(\_1位加扰 ), .sel(\随机信号_5_out ));
  assign \加扰后数据  = \随机加扰屏蔽字  ^ \_22位输入 ;  // XOR_Gate xor_3, 22 bits wide

  // Notes on the sheet:
  //   在随机加扰模式中增加三位错
  //   两个随机信号分别负责高16位和第16位
  //   加扰模式引脚00：不加扰  01:1位加扰 10:2位加扰 11：0-2位随机加扰
  //   如果两个信号相同，其中一个移位
  //   contents of rom_1 (hex, n*v repeats v):
  //   2 2 1 1 1 4*0 4*2 1 1 1 0 1 0 0 2 0 2 5*0 1 0 1 4*0 2
endmodule
