// Logisim project 1.circ as structural Verilog: 3 circuits, main circuit 输入输出测试
module \线路测试  (
  input  in_1,
  input  [7:0] in_2,
  input  [31:0] in_3,
  output [15:0] out_4,
  output [3:0] out_5,
  output [3:0] out_6,
  output [3:0] out_7
);

  // Probe on out_4
  assign out_4 = {{8{in_2[7]}}, in_2};  // Bit_Extender bit_extender_1

  assign out_5 = out_4[15:12];
  assign out_6 = out_4[9:6];
  assign out_7 = out_4[9:6];

  // Other names for the same wires on the sheet: _1[3:0] = out_4[9:6]
endmodule

module \逻辑门  (
  input  in_1,
  input  in_2,
  output out_3
);

  xor xor_1 (out_3, in_1, in_2);
endmodule

module \输入输出测试  (
  input  \读使能 ,
  input  \清除缓冲区 ,
  input  \写使能 ,
  input  \清除屏幕 ,
  output \缓冲区状态 
);

  wire clock_1_out;
  wire [6:0] keyboard_1_data;

  Clock clock_1 (.out(clock_1_out));
  Keyboard keyboard_1 (.clk(clock_1_out), .re(\读使能 ), .clr(\清除缓冲区 ), .avail(\缓冲区状态 ), .data(keyboard_1_data));
  TTY tty_1 (.data(keyboard_1_data), .clk(clock_1_out), .we(\写使能 ), .clr(\清除屏幕 ));
endmodule
