// Logisim project 4bit_adder_parallel.circ as structural Verilog: 1 circuit, main circuit 4bit_adder_parallel
module _4bit_adder_parallel (
  input  [3:0] X,
  input  [3:0] Y,
  input  C0,
  output [3:0] S,
  output C4,
  output C3
);

  wire and_1_out, and_2_out, and_3_out, and_4_out, and_5_out, and_6_out, and_7_out, and_8_out, or_3_out,
       or_4_out, xor_2_out, xor_3_out, xor_5_out, xor_8_out;

  or or_1 (C4, and_1_out, and_2_out);
  and and_1 (and_1_out, C3, xor_2_out);
  and and_2 (and_2_out, X[3], Y[3]);
  xor xor_1 (S[3], C3, xor_2_out);
  or or_2 (C3, and_3_out, and_4_out);
  xor xor_2 (xor_2_out, Y[3], X[3]);
  and and_3 (and_3_out, or_3_out, xor_3_out);
  and and_4 (and_4_out, X[2], Y[2]);
  xor xor_3 (xor_3_out, Y[2], X[2]);
  xor xor_4 (S[2], or_3_out, xor_3_out);
  or or_3 (or_3_out, and_6_out, and_5_out);
  and and_5 (and_5_out, X[1], Y[1]);
  and and_6 (and_6_out, or_4_out, xor_5_out);
  xor xor_5 (xor_5_out, Y[1], X[1]);
  xor xor_6 (S[1], or_4_out, xor_5_out);
  and and_7 (and_7_out, C0, xor_8_out);
  or or_4 (or_4_out, and_7_out, and_8_out);
  and and_8 (and_8_out, X[0], Y[0]);
  // Probe on X
  // Probe on Y
  // Probe on S
  xor xor_7 (S[0], xor_8_out, C0);
  xor xor_8 (xor_8_out, Y[0], X[0]);
  // Probe on X
  // Probe on Y
  // Probe on S

  // Notes on the sheet:
  //   X: pull=down
  //   Y: pull=down
  //   C0: pull=down
  //   输入引脚区
  //   4位快速加法器
  //   输出引脚区
  //   功能说明:4位Adder  S=X+Y，C4、C3分别为最高位、次高位进位位，C0为进位输入
  //   +
  //   =
  //   有符号加法
  //   +
  //   =
  //   无符号加法
endmodule
