// Logisim project 8bit_adder_examine.circ as structural Verilog: 1 circuit, main circuit 8bit_adder_examine
module _8bit_adder_examine (
  input  [7:0] A,
  input  [7:0] B,
  input  Sub,
  input  [1:0] in_4,
  input  [1:0] in_5,
  output [7:0] S,
  output Cout,
  output Overflow
);

  wire _4bit_adder_out_4, and_1_out, bitselector_1_out, bitselector_2_out;
  wire [3:0] demultiplexer_1_out0, demultiplexer_1_out1, demultiplexer_2_out0, demultiplexer_2_out1,
       multiplexer_1_out, multiplexer_2_out, not_1_out, not_2_out;

  Demultiplexer #(.width(4), .enable("false")) demultiplexer_1 (
    .out0(demultiplexer_1_out0), .out1(demultiplexer_1_out1), .in(B[3:0]), .sel(Sub));
  assign not_1_out = ~demultiplexer_1_out1;  // NOT_Gate not_1, 4 bits wide
  Multiplexer #(.width(4), .enable("false")) multiplexer_1 (
    .in0(demultiplexer_1_out0), .in1(not_1_out), .out(multiplexer_1_out), .sel(Sub));
  _4bit_adder _4bit_adder (
    .in_1(A[3:0]), .in_2(Sub), .in_3(multiplexer_1_out), .out_4(_4bit_adder_out_4), .out_5(S[3:0]));
  Demultiplexer #(.width(4), .enable("false")) demultiplexer_2 (
    .out0(demultiplexer_2_out0), .out1(demultiplexer_2_out1), .in(B[7:4]), .sel(Sub));
  _4bit_adder _4bit_adder_2 (
    .in_1(A[7:4]), .in_2(_4bit_adder_out_4), .in_3(multiplexer_2_out), .out_4(Cout), .out_5(S[7:4]));
  Multiplexer #(.width(4), .enable("false")) multiplexer_2 (
    .in0(demultiplexer_2_out0), .in1(not_2_out), .out(multiplexer_2_out), .sel(Sub));
  assign not_2_out = ~demultiplexer_2_out1;  // NOT_Gate not_2, 4 bits wide
  BitSelector #(.width(4)) bitselector_1 (.in(A[7:4]), .out(bitselector_1_out), .sel(in_5));
  // Probe on A
  // Probe on B
  // Probe on S
  BitSelector #(.width(4)) bitselector_2 (.in(B[7:4]), .out(bitselector_2_out), .sel(in_4));
  and and_1 (and_1_out, bitselector_1_out, bitselector_2_out);
  // Probe on A
  // Probe on B
  // Probe on S
  xor xor_1 (Overflow, and_1_out, Cout);

  // Other names for the same wires on the sheet: A0_nA3[3:0] = A[3:0]; A4_nA7[3:0] = A[7:4]; B0_nB3[3:0] = B[3:0];
  //   B4_nB7[3:0] = B[7:4]; OF = Overflow; S0_nS3[3:0] = S[3:0]; S4_nS7[3:0] = S[7:4]

  // Notes on the sheet:
  //   Cout: pull=down
  //   B: pull=down
  //   Sub: pull=down
  //   A: pull=down
  //   Overflow: pull=down
  //   S: pull=down
  //   输入引脚区
  //   输出引脚区
  //   功能说明：  8位可控加减法器    Sub=0: S = A＋B  Sub=1:S = A－B   Cout为最高位进位位，Overflow为有符号溢出标志
  //   =
  //   有符号
  //   =
  //   无符号
endmodule
