// Logisim project full_adder.circ as structural Verilog: 3 circuits, main circuit full_adder
module full_adder (
  input  in_1,
  input  in_2,
  input  in_3,
  output out_4,
  output out_5
);

  wire and_1_out, and_2_out, xor_1_out;

  xor xor_1 (xor_1_out, in_1, in_2);
  and and_1 (and_1_out, in_1, in_2);
  and and_2 (and_2_out, xor_1_out, in_3);
  or or_1 (out_4, and_2_out, and_1_out);
  xor xor_2 (out_5, xor_1_out, in_3);
endmodule

module _4bit_adder (
  input  [3:0] in_1,
  input  in_2,
  input  [3:0] in_3,
  output out_4,
  output [3:0] out_5
);

  wire full_adder_1_out_4, full_adder_2_out_4, full_adder_3_out_4;

  // Probe on in_1
  // Probe on in_3
  full_adder full_adder_1 (.in_1(in_2), .in_2(in_1[0]), .in_3(in_3[0]), .out_4(full_adder_1_out_4), .out_5(out_5[0]));
  full_adder full_adder_2 (
    .in_1(full_adder_1_out_4), .in_2(in_1[1]), .in_3(in_3[1]), .out_4(full_adder_2_out_4), .out_5(out_5[1]));
  full_adder full_adder_3 (
    .in_1(full_adder_2_out_4), .in_2(in_1[2]), .in_3(in_3[2]), .out_4(full_adder_3_out_4), .out_5(out_5[2]));
  full_adder full_adder_4 (.in_1(full_adder_3_out_4), .in_2(in_1[3]), .in_3(in_3[3]), .out_4(out_4), .out_5(out_5[3]));
  // Probe on out_5
endmodule

module _8bit_adder (
  input  [7:0] in_1,
  input  in_2,
  input  [7:0] in_3,
  output out_4,
  output [7:0] out_5
);

  wire _4bit_adder_out_4;

  // Probe on in_1
  // Probe on in_3
  _4bit_adder _4bit_adder (
    .in_1(in_1[3:0]), .in_2(in_2), .in_3(in_3[3:0]), .out_4(_4bit_adder_out_4), .out_5(out_5[3:0]));
  _4bit_adder _4bit_adder_2 (
    .in_1(in_1[7:4]), .in_2(_4bit_adder_out_4), .in_3(in_3[7:4]), .out_4(out_4), .out_5(out_5[7:4]));
  // Probe on out_5
endmodule
