// Logisim project 8b_controlable_addsuber.circ as structural Verilog: 1 circuit, main circuit main
module main (
  input  [7:0] A,
  input  [7:0] B,
  input  Sub,
  input  Cin,
  output [7:0] S,
  output Cout,
  output Overflow
);

  wire n4bit_adder_parallel_1_c3, n4bit_adder_parallel_2_c4, xor_9_out;
  wire [3:0] xor_4_out, xor_8_out;

  xor xor_1 (xor_4_out[3], B[7], Sub);
  xor xor_2 (xor_4_out[2], B[6], Sub);
  xor xor_3 (xor_4_out[1], B[5], Sub);
  xor xor_4 (xor_4_out[0], B[4], Sub);
  _4bit_adder_parallel u_4bit_adder_parallel_1 (
    .X(xor_4_out), .Y(A[7:4]), .C0(n4bit_adder_parallel_2_c4), .S(S[7:4]), .C4(Cout),
    .C3(n4bit_adder_parallel_1_c3));
  xor xor_5 (xor_8_out[3], B[3], Sub);
  xnor xnor_1 (Overflow, Cout, n4bit_adder_parallel_1_c3);
  xor xor_6 (xor_8_out[2], B[2], Sub);
  // Probe on A
  // Probe on B
  // Probe on Cin
  // Probe on S
  xor xor_7 (xor_8_out[1], B[1], Sub);
  xor xor_8 (xor_8_out[0], B[0], Sub);
  // Probe on A
  // Probe on B
  // Probe on Cin
  // Probe on S
  _4bit_adder_parallel u_4bit_adder_parallel_2 (
    .X(xor_8_out), .Y(A[3:0]), .C0(xor_9_out), .S(S[3:0]), .C4(n4bit_adder_parallel_2_c4));  // open: C3
  xor xor_9 (xor_9_out, Sub, Cin);

  // Other names for the same wires on the sheet: A0_A3[3:0] = A[3:0]; A4_A7[3:0] = A[7:4]; B0_B3[3:0] = B[3:0];
  //   B4_B7[3:0] = B[7:4]; OF = Overflow

  // Notes on the sheet:
  //   A: pull=down
  //   S: pull=down
  //   Cout: pull=down
  //   Overflow: pull=down
  //   B: pull=down
  //   Sub: pull=down
  //   Cin: pull=down
  //   输入引脚区
  //   Cout为最高位进位位，Overflow为有符号溢出标志
  //   输出引脚区
  //   功能说明：8位可控加减法器    Sub=0 Cin=0: S=A+B；Sub=0 Cin=1: S=A+B+1；Sub=1 Cin=0: S=A-B；Sub=1 Cin=1: S=A-B-1。
  //   =
  //   有符号
  //   =
  //   无符号
endmodule
