// Logisim project ALU.circ as structural Verilog: 1 circuit, main circuit main
module main (
  input  [2:0] in_1,
  input  [7:0] A,
  input  [7:0] B,
  input  [1:0] S1S0,
  input  Cin,
  input  S2,
  input  S3,
  output [7:0] Y,
  output CA,
  output ZO,
  output SG,
  output OV,
  output [2:0] out_13
);

  wire main_1_out_4, main_3_cout;
  wire [6:0] main_3_s;
  wire [7:0] main_1_out_5, main_2_out_4, multiplexer_1_out;

  // Probe on A
  // Probe on B
  SOL_main main_1 (.B(B), .shift_num(in_1), .S1S0(S1S0), .out_4(main_1_out_4), .out_5(main_1_out_5));
  logical_computer_main main_2 (.A(A), .B(B), .S1S0(S1S0), .out_4(main_2_out_4));
  _8b_controlable_addsuber_main main_3 (
    .A(A), .B(B), .Sub(S1S0[0]), .Cin(Cin), .S({SG, main_3_s}), .Cout(main_3_cout), .Overflow(OV));
  Comparator comparator_1 (.a(A), .b(B), .gt(out_13[0]), .eq(out_13[1]), .lt(out_13[2]));
  Multiplexer #(.width(8), .enable("false")) multiplexer_1 (
    .in0({SG, main_3_s}), .in1(main_2_out_4), .out(multiplexer_1_out), .sel(S2));
  // Probe on Y
  Multiplexer #(.width(8), .enable("false")) multiplexer_2 (
    .in0(main_1_out_5), .in1(multiplexer_1_out), .out(Y), .sel(S3));
  nor nor_1 (ZO, multiplexer_1_out[7], multiplexer_1_out[6], multiplexer_1_out[5], multiplexer_1_out[4], multiplexer_1_out[3], multiplexer_1_out[2], multiplexer_1_out[1], multiplexer_1_out[0]);
  Multiplexer #(.enable("false")) multiplexer_3 (.in0(main_1_out_4), .in1(main_3_cout), .out(CA), .sel(S3));
endmodule
