// Logisim project SOL.circ as structural Verilog: 1 circuit, main circuit main
module main (
  input  [7:0] B,
  input  [2:0] shift_num,
  input  [1:0] S1S0,
  output out_4,
  output [7:0] out_5
);

  wire [7:0] shifter_1_out, shifter_2_out, shifter_3_out;

  Shifter shifter_1 (.in(B), .\dist (shift_num), .out(shifter_1_out));
  Shifter #(.shift("lr")) shifter_2 (.in(B), .\dist (shift_num), .out(shifter_2_out));
  Shifter #(.shift("ar")) shifter_3 (.in(B), .\dist (shift_num), .out(shifter_3_out));
  Multiplexer #(.select(2), .width(8)) multiplexer_1 (
    .in0(B), .in1(shifter_1_out), .in2(shifter_2_out), .in3(shifter_3_out), .out(out_5), .sel(S1S0));  // open: en

  assign out_4 = B[7];
endmodule
