// Logisim project 加减法验证电路.circ as structural Verilog: 1 circuit, main circuit main
module main (
  input  [7:0] A,
  input  [7:0] B,
  input  Sub,
  input  Cin,
  output [7:0] S,
  output Cout,
  output Overflow
);

  // Probe on A
  // Probe on B
  // Probe on Cin
  // Probe on S
  // Probe on A
  // Probe on B
  // Probe on Cin
  // Probe on S

  // Other names for the same wires on the sheet: OF = Overflow

  // Notes on the sheet:
  //   Sub: pull=down
  //   Overflow: pull=down
  //   Cout: pull=down
  //   B: pull=down
  //   Cin: pull=down
  //   S: pull=down
  //   A: pull=down
  //   输入引脚区
  //   Cout为最高位进位位，Overflow为有符号溢出标志
  //   输出引脚区
  //   功能说明：8位可控加减法器    Sub=0 Cin=0: S=A+B；Sub=0 Cin=1: S=A+B+1；Sub=1 Cin=0: S=A-B；Sub=1 Cin=1: S=A-B-1。
  //   =
  //   有符号
  //   =
  //   无符号
endmodule
