// Logisim project 全加器1位.circ as structural Verilog: 5 circuits, main circuit main
module main (
  input  O1,
  input  O2,
  input  cin,
  output S,
  output cout
);

  wire and_1_out, and_2_out, xor_1_out;

  xor xor_1 (xor_1_out, O1, O2);
  and and_1 (and_1_out, O1, O2);
  xor xor_2 (S, xor_1_out, cin);
  and and_2 (and_2_out, xor_1_out, cin);
  or or_1 (cout, and_2_out, and_1_out);
endmodule

module \全加器四位  (
  input  [3:0] O1,
  input  [3:0] O2,
  input  cin,
  output \第五位 ,
  output SF,
  output \溢出标志 ,
  output [3:0] Cout
);

  wire main_2_cout, main_3_cout, main_4_cout;

  xor xor_1 (\溢出标志 , \第五位 , main_2_cout);
  main main_1 (.O1(O1[3]), .O2(O2[3]), .cin(main_2_cout), .S(Cout[3]), .cout(\第五位 ));
  main main_2 (.O1(O1[2]), .O2(O2[2]), .cin(main_3_cout), .S(Cout[2]), .cout(main_2_cout));
  main main_3 (.O1(O1[1]), .O2(O2[1]), .cin(main_4_cout), .S(Cout[1]), .cout(main_3_cout));
  main main_4 (.O1(O1[0]), .O2(O2[0]), .cin(cin), .S(Cout[0]), .cout(main_4_cout));

  assign SF = Cout[3];
endmodule

module \全加器八位  (
  input  [7:0] O1,
  input  [7:0] O2,
  input  in_3,
  output out_4,
  output \溢出 ,
  output [7:0] Cout
);

  wire \全加器四位_1_溢出标志 , \全加器四位_2_溢出标志 , \全加器四位_2_第五位 ;

  or or_1 (\溢出 , \全加器四位_1_溢出标志 , \全加器四位_2_溢出标志 );
  \全加器四位  \u_全加器四位_1  (
    .\第五位 (out_4), .\溢出标志 (\全加器四位_1_溢出标志 ), .cin(\全加器四位_2_第五位 ), .O1(O1[7:4]), .O2(O2[7:4]), .Cout(Cout[7:4]));  // open: SF
  \全加器四位  \u_全加器四位_2  (
    .\第五位 (\全加器四位_2_第五位 ), .\溢出标志 (\全加器四位_2_溢出标志 ), .cin(in_3), .O1(O1[3:0]), .O2(O2[3:0]), .Cout(Cout[3:0]));  // open: SF
endmodule

module \全减器  (
  input  O1,
  input  O2,
  input  Cin,
  input  \加减控制 ,
  output S,
  output cout
);

  wire and_1_out, and_2_out, and_3_out, xor_1_out, xor_2_out;

  xor xor_1 (xor_1_out, O1, \加减控制 );
  and and_1 (and_1_out, O2, O2, xor_1_out);
  and and_2 (and_2_out, O2, Cin);
  and and_3 (and_3_out, Cin, xor_1_out);
  xor xor_2 (xor_2_out, O1, O2);
  xor xor_3 (S, xor_2_out, Cin);
  or or_1 (cout, and_1_out, and_2_out, and_3_out);
endmodule

module \四位快速加法器  (
  input  P1,
  input  P2,
  input  P3,
  input  P4,
  input  G1,
  input  G2,
  input  G3,
  input  G4,
  input  Cin,
  output C1,
  output C2,
  output C3,
  output P_star,
  output C4,
  output G_star
);

  wire and_1_out, and_2_out, and_3_out, and_4_out, and_5_out, and_6_out, and_7_out, and_9_out, and_10_out,
       and_11_out;

  and and_1 (and_1_out, Cin, P1);
  or or_1 (C1, and_1_out, G1);
  and and_2 (and_2_out, Cin, P1, P2);
  or or_2 (C2, and_2_out, G2, and_3_out);
  and and_3 (and_3_out, G1, P2);
  and and_4 (and_4_out, P2, G1, P3);
  and and_5 (and_5_out, Cin, P1, P2, P3);
  or or_3 (C3, and_5_out, and_4_out, and_6_out, G3);
  and and_6 (and_6_out, P3, G2);
  and and_7 (and_7_out, Cin, P1, P2, P3, P4);
  and and_8 (P_star, P1, P2, P3, P4);
  and and_9 (and_9_out, G1, P2, P3, P4);
  or or_4 (C4, and_7_out, and_9_out, G4, and_10_out, and_11_out);
  and and_10 (and_10_out, G2, P3, P4);
  and and_11 (and_11_out, P4, G3);
  or or_5 (G_star, and_11_out, and_10_out, and_9_out, G4);
endmodule
