// Logisim project 加法器验证电路.circ as structural Verilog: 2 circuits, main circuit 4位并行加法器验证电路
module \_4位并行加法器验证电路  (
  input  [3:0] X,
  input  [3:0] Y,
  input  C0,
  output [3:0] S,
  output C4,
  output C3
);

  wire and_1_out, and_2_out, and_3_out, and_4_out, xor_2_out, xor_3_out, xor_5_out, xor_8_out;

  and and_1 (and_1_out, X[3], Y[3]);
  xor xor_1 (S[3], C3, xor_2_out);
  xor xor_2 (xor_2_out, Y[3], X[3]);
  xor xor_3 (xor_3_out, Y[2], X[2]);
  and and_2 (and_2_out, X[2], Y[2]);
  buf xor_4 (S[2], xor_3_out);  // XOR_Gate
  and and_3 (and_3_out, X[1], Y[1]);
  // 四位快速加法器 四位快速加法器_1: pin names not known
  xor xor_5 (xor_5_out, Y[1], X[1]);
  buf xor_6 (S[1], xor_5_out);  // XOR_Gate
  and and_4 (and_4_out, X[0], Y[0]);
  // Probe on X
  // Probe on Y
  // Probe on S
  xor xor_7 (S[0], xor_8_out, C0);
  xor xor_8 (xor_8_out, Y[0], X[0]);
  // Probe on X
  // Probe on Y
  // Probe on S

  // Notes on the sheet:
  //   X: pull=down
  //   Y: pull=down
  //   C0: pull=down
  //   输入引脚区
  //   4位快速加法器
  //   输出引脚区
  //   功能说明:4位Adder  S=X+Y，C4、C3分别为最高位、次高位进位位，C0为进位输入
  //   +
  //   =
  //   有符号加法
  //   +
  //   =
  //   无符号加法
endmodule

module \_8位加法器验证电路  (
  input  [7:0] A,
  input  [7:0] B,
  input  Sub,
  output [7:0] S,
  output Cout,
  output Overflow
);

  // Probe on A
  // Probe on B
  // Probe on S
  // Probe on A
  // Probe on B
  // Probe on S

  // Other names for the same wires on the sheet: A0_nA3[3:0] = A[3:0]; A4_nA7[3:0] = A[7:4]; B0_nB3[3:0] = B[3:0];
  //   B4_nB7[3:0] = B[7:4]; OF = Overflow; S0_nS3[3:0] = S[3:0]; S4_nS7[3:0] = S[7:4]

  // Notes on the sheet:
  //   S: pull=down
  //   Overflow: pull=down
  //   Cout: pull=down
  //   Sub: pull=down
  //   A: pull=down
  //   B: pull=down
  //   输入引脚区
  //   输出引脚区
  //   功能说明：  8位可控加减法器    Sub=0: S = A＋B  Sub=1:S = A－B   Cout为最高位进位位，Overflow为有符号溢出标志
  //   =
  //   有符号
  //   =
  //   无符号
endmodule
