// Logisim project 控制器.circ as structural Verilog: 8 circuits, main circuit main
module main (
  input  Reset,
  input  [1:0] in_2
);

  wire CLK_2_t0, CLK_2_t1, CLK_2_t2, CLK_2_t3, CLK_out, cu_1_jc, cu_1_jp, cu_1_jz, \cu_1_r_w读或写 ,
       \cu_1_rm读内存 , \cu_1_s_b_i选择b或者立即数 , \cu_1_wm写内存 , en, JC_P_Z;
  wire [1:0] \cu_1_s_regs选择寄存器 ;
  wire [3:0] ALU_ca, \立即数 ;
  wire [3:2] \cu_1_s_regs选择寄存器_2 ;
  wire [4:0] \cu_1_s_op运算选择 ;
  wire [7:0] ALU_out_8, cu_1_p_address, Flagl, FO, multiplexer_2_out, ram_1_data, re, Regs_a_tunnel,
       Regs_b_tunnel, \s_b_i_1_加法器b通道输入 ;
  wire [15:0] rom_1_data;

  Clock CLK (.out(CLK_out));
  not not_1 (en, rom_1_data[0]);
  CLK CLK_2 (.CLK(CLK_out), .Reset(Reset), .T0(CLK_2_t0), .T1(CLK_2_t1), .T2(CLK_2_t2), .T3(CLK_2_t3));
  // Probe on \cu_1_s_regs选择寄存器_2 
  ROM #(.dataWidth(16)) rom_1 (.addr(cu_1_p_address), .data(rom_1_data));  // open: sel
  // Probe on \立即数 
  Register register_1 (.D(Flagl), .en(en), .Q(FO), .clk(CLK_2_t2));  // open: clr
  assign re = {{4{1'b0}}, \立即数 };  // Bit_Extender bit_extender_1
  // Probe on {\cu_1_s_regs选择寄存器_2 , \cu_1_s_regs选择寄存器 , \立即数 }
  Reg Regs (
    .data(multiplexer_2_out), .C_Reg(\cu_1_s_regs选择寄存器_2 ), .R_W(\cu_1_r_w读或写 ), .CLK(CLK_2_t2),
    .SA(\cu_1_s_regs选择寄存器 ), .SB(\立即数 [3:2]), .A_tunnel(Regs_a_tunnel), .B_tunnel(Regs_b_tunnel));
  // Probe on Regs_b_tunnel
  // Probe on \cu_1_r_w读或写 
  CU cu_1 (
    .\TC切换下一 (CLK_2_t0), .\RES复位 (Reset), .\偏移量 (re), .\置0默认加1 (JC_P_Z), .\I_in指令入口 (rom_1_data),
    .\TF取值使能 (CLK_2_t1), .Z(FO[0]), .C(FO[1]), .S(FO[2]), .P_address(cu_1_p_address),
    .\R_W读或写 (\cu_1_r_w读或写 ), .\S_B_I选择B或者立即数 (\cu_1_s_b_i选择b或者立即数 ), .\RM读内存 (\cu_1_rm读内存 ),
    .\WM写内存 (\cu_1_wm写内存 ), .JP(cu_1_jp), .JZ(cu_1_jz), .JC(cu_1_jc), .\S_op运算选择 (\cu_1_s_op运算选择 ),
    .\S_Regs选择寄存器 ({\cu_1_s_regs选择寄存器_2 , \cu_1_s_regs选择寄存器 , \立即数 }));
  S_B_I s_b_i_1 (
    .\B通道输出 (Regs_b_tunnel), .\_4位立即数 (\立即数 ), .\S_B_I选择数 (\cu_1_s_b_i选择b或者立即数 ),
    .\加法器B通道输入 (\s_b_i_1_加法器b通道输入 ));
  Multiplexer #(.select(2)) multiplexer_1 (
    .in0(1'b0), .in1(cu_1_jp), .in2(cu_1_jz), .in3(cu_1_jc), .out(JC_P_Z), .sel(in_2));  // open: en
  // Probe on \s_b_i_1_加法器b通道输入 
  // Probe on \cu_1_s_op运算选择 
  RAM #(.bus("separate")) ram_1 (
    .addr(Regs_a_tunnel), .din(\s_b_i_1_加法器b通道输入 ), .data(ram_1_data), .str(\cu_1_wm写内存 ), .clk(CLK_2_t3));  // open: sel, ld, clr
  // Probe on Regs_a_tunnel
  ALU_main ALU (
    .A(Regs_a_tunnel), .B(\s_b_i_1_加法器b通道输入 ), .N(3'b001), .S(\cu_1_s_op运算选择 [2:1]),
    .cin(\cu_1_s_op运算选择 [0]), .S2(\cu_1_s_op运算选择 [3]), .S3(\cu_1_s_op运算选择 [4]), .out_8(ALU_out_8),
    .CA(ALU_ca[0]), .OV(ALU_ca[1]), .SG(ALU_ca[2]), .ZO(ALU_ca[3]));
  // Probe on ALU_out_8
  ROM #(.dataWidth(16)) rom_2 ();  // open: addr, data, sel
  assign Flagl = {{4{1'b0}}, ALU_ca};  // Bit_Extender bit_extender_2
  Multiplexer #(.width(8)) multiplexer_2 (
    .in0(ALU_out_8), .in1(ram_1_data), .out(multiplexer_2_out), .sel(\cu_1_rm读内存 ));  // open: en
  ROM #(.dataWidth(16)) rom_3 ();  // open: addr, data, sel

  // Notes on the sheet:
  //   solve: -8*10
  //   contents of rom_1 (hex, n*v repeats v):
  //   2008 40 20c0 200 244 244 244 1084 4038 7*0 1010
  //   solve: -8/4
  //   contents of rom_2 (hex, n*v repeats v):
  //   2008 600 600
  //   febonacci
  //   contents of rom_3 (hex, n*v repeats v):
  //   2001 2041 20c0 1084 4038 15fc 4 58 800b
endmodule

module Reg (
  input  [7:0] data,
  input  [1:0] C_Reg,
  input  R_W,
  input  CLK,
  input  [1:0] SA,
  input  [1:0] SB,
  output [7:0] A_tunnel,
  output [7:0] B_tunnel
);

  wire and_1_out, and_2_out, and_3_out, and_4_out, decoder_1_out0, decoder_1_out1, decoder_1_out2,
       decoder_1_out3;
  wire [7:0] R0_q, R1_q, R2_q, R3_q;

  Decoder #(.select(2)) decoder_1 (
    .out0(decoder_1_out0), .out1(decoder_1_out1), .out2(decoder_1_out2), .out3(decoder_1_out3), .sel(C_Reg));  // open: en
  // Probe on data
  and and_1 (and_1_out, decoder_1_out0, R_W);
  and and_2 (and_2_out, decoder_1_out1, R_W);
  and and_3 (and_3_out, decoder_1_out2, R_W);
  and and_4 (and_4_out, decoder_1_out3, R_W);
  Register R0 (.D(data), .en(and_1_out), .Q(R0_q), .clk(CLK));  // open: clr
  Register R1 (.D(data), .en(and_2_out), .Q(R1_q), .clk(CLK));  // open: clr
  Register R2 (.D(data), .en(and_3_out), .Q(R2_q), .clk(CLK));  // open: clr
  Register R3 (.D(data), .en(and_4_out), .Q(R3_q), .clk(CLK));  // open: clr
  Multiplexer #(.select(2), .width(8)) multiplexer_1 (
    .in0(R0_q), .in1(R1_q), .in2(R2_q), .in3(R3_q), .out(A_tunnel), .sel(SA));  // open: en
  Multiplexer #(.select(2), .width(8)) multiplexer_2 (
    .in0(R0_q), .in1(R1_q), .in2(R2_q), .in3(R3_q), .out(B_tunnel), .sel(SB));  // open: en
endmodule

module PC (
  input  \TC切换下一 ,
  input  \RES复位 ,
  input  [7:0] \偏移量 ,
  input  \置0默认加1 ,
  output [7:0] P_address
);

  wire [7:0] multiplexer_1_out, \n8位加减法器_1_s ;

  Register register_1 (.D(\n8位加减法器_1_s ), .Q(P_address), .clk(\TC切换下一 ), .clr(\RES复位 ));  // open: en
  Multiplexer #(.width(8)) multiplexer_1 (
    .in0(8'h1), .in1(\偏移量 ), .out(multiplexer_1_out), .sel(\置0默认加1 ));  // open: en
  \_8位加减法器  \u_8位加减法器_1  (
    .A(multiplexer_1_out), .B(P_address), .S(\n8位加减法器_1_s ), .Sub(1'b0), .Cin(1'b0));  // open: upper, SF, OF
endmodule

module IR_ID (
  input  [15:0] \I_in指令入口 ,
  input  \TF取值使能 ,
  output \R_W读或写 ,
  output \S_B_I选择B或者立即数 ,
  output \RM读内存 ,
  output \WM写内存 ,
  output JP,
  output JZ,
  output JC,
  output [4:0] \S_op运算选择 ,
  output [7:0] \S_Regs选择寄存器 
);

  wire [15:13] register_1_q;

  Register #(.width(16)) register_1 (
    .D(\I_in指令入口 ), .Q({register_1_q, \S_op运算选择 , \S_Regs选择寄存器 }), .clk(\TF取值使能 ));  // open: en, clr
  \_38译码器  \u_38译码器_1  (
    .X(register_1_q[15]), .Y(register_1_q[14]), .Z(register_1_q[13]), .R_W(\R_W读或写 ), .SB(\S_B_I选择B或者立即数 ),
    .RM(\RM读内存 ), .WM(\WM写内存 ), .ZP(JP), .JZ(JZ), .JC(JC));

  // Notes on the sheet:
  //   IR指令储存器
endmodule

module \_38译码器  (
  input  X,
  input  Y,
  input  Z,
  output R_W,
  output SB,
  output RM,
  output WM,
  output ZP,
  output JZ,
  output JC
);

  wire and_1_out, and_2_out, and_3_out, and_4_out, not_1_out, not_2_out, not_3_out, not_4_out, not_5_out,
       not_6_out, not_7_out, not_8_out, not_9_out, not_10_out, not_11_out, not_12_out;

  not not_1 (not_1_out, X);
  not not_2 (not_2_out, Y);
  not not_3 (not_3_out, X);
  not not_4 (not_4_out, Y);
  not not_5 (not_5_out, Z);
  not not_6 (not_6_out, X);
  not not_7 (not_7_out, X);
  not not_8 (not_8_out, Z);
  not not_9 (not_9_out, Y);
  not not_10 (not_10_out, Z);
  not not_11 (not_11_out, Y);
  not not_12 (not_12_out, Z);
  and and_1 (and_1_out, not_1_out, not_2_out);
  and and_2 (and_2_out, not_3_out, Z);
  and and_3 (and_3_out, not_4_out, Z);
  and and_4 (and_4_out, X, not_5_out);
  and and_5 (RM, not_6_out, Y, Z);
  and and_6 (WM, not_7_out, Y, not_8_out);
  and and_7 (ZP, X, not_9_out, not_10_out);
  and and_8 (JZ, X, not_11_out, Z);
  and and_9 (JC, X, Y, not_12_out);
  or or_1 (R_W, and_1_out, and_2_out);
  or or_2 (SB, and_3_out, and_4_out);
endmodule

module CLK (
  input  CLK,
  input  Reset,
  output T0,
  output T1,
  output T2,
  output T3
);

  wire [1:0] counter_1_q;

  Demultiplexer #(.select(2)) demultiplexer_1 (
    .out0(T0), .out1(T1), .out2(T2), .out3(T3), .in(1'b1), .sel(counter_1_q));  // open: en
  Counter #(.width(2), .max('h3)) counter_1 (.Q(counter_1_q), .clk(CLK), .clr(Reset));  // open: load, D, count, carry
endmodule

module S_B_I (
  input  [7:0] \B通道输出 ,
  input  [3:0] \_4位立即数 ,
  input  \S_B_I选择数 ,
  output [7:0] \加法器B通道输入 
);

  wire [7:0] bit_extender_1_out;

  // Probe on \_4位立即数 
  assign bit_extender_1_out = {{4{\_4位立即数 [3]}}, \_4位立即数 };  // Bit_Extender bit_extender_1
  Multiplexer #(.width(8)) multiplexer_1 (
    .in0(\B通道输出 ), .in1(bit_extender_1_out), .out(\加法器B通道输入 ), .sel(\S_B_I选择数 ));  // open: en
  // Probe on \加法器B通道输入 
endmodule

module CU (
  input  \TC切换下一 ,
  input  \RES复位 ,
  input  [7:0] \偏移量 ,
  input  \置0默认加1 ,
  input  [15:0] \I_in指令入口 ,
  input  \TF取值使能 ,
  input  Z,
  input  C,
  input  S,
  output [7:0] P_address,
  output \R_W读或写 ,
  output \S_B_I选择B或者立即数 ,
  output \RM读内存 ,
  output \WM写内存 ,
  output JP,
  output JZ,
  output JC,
  output [4:0] \S_op运算选择 ,
  output [7:0] \S_Regs选择寄存器 
);

  PC pc_1 (.\TC切换下一 (\TC切换下一 ), .\RES复位 (\RES复位 ), .\偏移量 (\偏移量 ), .\置0默认加1 (\置0默认加1 ), .P_address(P_address));
  IR_ID ir_id_1 (
    .\I_in指令入口 (\I_in指令入口 ), .\TF取值使能 (\TF取值使能 ), .\R_W读或写 (\R_W读或写 ), .\S_B_I选择B或者立即数 (\S_B_I选择B或者立即数 ),
    .\RM读内存 (\RM读内存 ), .\WM写内存 (\WM写内存 ), .JP(JP), .JZ(JZ), .JC(JC), .\S_op运算选择 (\S_op运算选择 ),
    .\S_Regs选择寄存器 (\S_Regs选择寄存器 ));
endmodule
