// Logisim project ALU.circ as structural Verilog: 4 circuits, main circuit main
module main (
  input  [7:0] A,
  input  [7:0] B,
  input  [2:0] N,
  input  [1:0] S,
  input  cin,
  input  S2,
  input  S3,
  output A_B,
  output A__B,
  output A_B_2,
  output [7:0] cout,
  output CA,
  output OV,
  output SG,
  output ZO
);

  wire \n8位加减法器_1_sf , not_2_out, \移位运算_1_sol ;
  wire [7:0] bit_extender_1_out, multiplexer_1_out, \n8位加减法器_1_s , nor_1_out, not_1_out, sub_B, \移位运算_1_y ,
       \逻辑运算_1_y ;
  wire [7:7] comparator_1_eq;

  // Probe on S[1]
  // Probe on A
  Comparator #(.width(1)) comparator_1 (.a(S[1]), .b(1'b1), .eq(comparator_1_eq[7]));  // open: gt, lt
  // Probe on B
  // Probe on comparator_1_eq[7]
  // Probe on comparator_1_eq[7]
  \移位运算  \u_移位运算_1  (.B(B), .N(N), .Select(S), .SOL(\移位运算_1_sol ), .Y(\移位运算_1_y ));
  \_8位加减法器  \u_8位加减法器_1  (
    .upper(SG), .SF(\n8位加减法器_1_sf ), .OF(OV), .A(sub_B), .B(A), .S(\n8位加减法器_1_s ), .Sub(S[0]), .Cin(cin));
  \逻辑运算  \u_逻辑运算_1  (.A(A), .B(B), .Select(S), .Y(\逻辑运算_1_y ));
  // Probe on B
  assign not_1_out = ~B;  // NOT_Gate not_1, 8 bits wide
  Multiplexer #(.width(8)) multiplexer_1 (
    .in0(\n8位加减法器_1_s ), .in1(\逻辑运算_1_y ), .out(multiplexer_1_out), .sel(S2));  // open: en
  // Probe on nor_1_out
  assign nor_1_out = ~(not_1_out | {8{comparator_1_eq[7]}});  // NOR_Gate nor_1, 8 bits wide
  assign bit_extender_1_out = {{7{1'b0}}, comparator_1_eq[7]};  // Bit_Extender bit_extender_1
  not not_2 (not_2_out, 1'b1);
  Multiplexer #(.width(8)) multiplexer_2 (.in0(\移位运算_1_y ), .in1(multiplexer_1_out), .out(cout), .sel(S3));  // open: en
  // Probe on sub_B
  \_8位加减法器  \u_8位加减法器_2  (
    .A(bit_extender_1_out), .B(nor_1_out), .S(sub_B), .Sub(not_2_out), .Cin(not_2_out));  // open: upper, SF, OF
  // Probe on cout
  Multiplexer multiplexer_3 (.in0(\移位运算_1_sol ), .in1(\n8位加减法器_1_sf ), .out(CA), .sel(S3));  // open: en
  Comparator comparator_2 (.a(A), .b(B), .gt(A_B), .eq(A__B), .lt(A_B_2));
  nor nor_2 (ZO, multiplexer_1_out[0], multiplexer_1_out[1], multiplexer_1_out[2], multiplexer_1_out[3], multiplexer_1_out[4], multiplexer_1_out[5], multiplexer_1_out[6], multiplexer_1_out[7]);

  // Other names for the same wires on the sheet: C1 = S[1]; sub_A[7:0] = B
endmodule

module \_8位加减法器  (
  input  [7:0] A,
  input  Sub,
  input  [7:0] B,
  input  Cin,
  output upper,
  output SF,
  output OF,
  output [7:0] S
);

  wire xor_9_out, \全加器四位_2_第五位 ;
  wire [3:0] xor_4_out, xor_8_out;

  xor xor_1 (xor_4_out[2], A[6], Sub);
  xor xor_2 (xor_4_out[3], A[7], Sub);
  xor xor_3 (xor_4_out[1], A[5], Sub);
  xor xor_4 (xor_4_out[0], A[4], Sub);
  \全加器四位  \u_全加器四位_1  (
    .\第五位 (upper), .SF(SF), .\溢出标志 (OF), .cin(\全加器四位_2_第五位 ), .O1(xor_4_out), .O2(B[7:4]), .Cout(S[7:4]));
  xor xor_5 (xor_8_out[3], A[3], Sub);
  xor xor_6 (xor_8_out[2], A[2], Sub);
  xor xor_7 (xor_8_out[1], A[1], Sub);
  xor xor_8 (xor_8_out[0], A[0], Sub);
  \全加器四位  \u_全加器四位_2  (
    .\第五位 (\全加器四位_2_第五位 ), .cin(xor_9_out), .O1(xor_8_out), .O2(B[3:0]), .Cout(S[3:0]));  // open: SF, 溢出标志
  xor xor_9 (xor_9_out, Sub, Cin);
endmodule

module \逻辑运算  (
  input  [7:0] A,
  input  [7:0] B,
  input  [1:0] Select,
  output [7:0] Y
);

  wire [7:0] and_1_out, not_1_out, or_1_out, xor_1_out;

  assign not_1_out = ~A;  // NOT_Gate not_1, 8 bits wide
  assign and_1_out = A & B;  // AND_Gate and_1, 8 bits wide
  assign or_1_out = A | B;  // OR_Gate or_1, 8 bits wide
  assign xor_1_out = A ^ B;  // XOR_Gate xor_1, 8 bits wide
  Multiplexer #(.select(2), .width(8)) multiplexer_1 (
    .in0(and_1_out), .in1(or_1_out), .in2(not_1_out), .in3(xor_1_out), .out(Y), .sel(Select));  // open: en
endmodule

module \移位运算  (
  input  [7:0] B,
  input  [2:0] N,
  input  [1:0] Select,
  output SOL,
  output [7:0] Y
);

  wire [7:0] shifter_1_out, shifter_2_out, shifter_3_out;

  Shifter shifter_1 (.in(B), .\dist (N), .out(shifter_1_out));
  Shifter #(.shift("lr")) shifter_2 (.in(B), .\dist (N), .out(shifter_2_out));
  Shifter #(.shift("ar")) shifter_3 (.in(B), .\dist (N), .out(shifter_3_out));
  Multiplexer #(.select(2), .width(8)) multiplexer_1 (
    .in0(B), .in1(shifter_1_out), .in2(shifter_2_out), .in3(shifter_3_out), .out(Y), .sel(Select));  // open: en

  assign SOL = B[7];
endmodule
