// Logisim project LED.circ as structural Verilog: 3 circuits, main circuit EncodedCirc
module main (
);

  wire button_1_out, button_2_out, button_3_out, button_4_out, button_5_out, encodedcirc_1_u,
       encodedcirc_1_x, encodedcirc_1_y, encodedcirc_1_z, main_1_out_6, main_1_out_7, main_1_out_8,
       main_1_out_9, main_1_out_10, n7_segment_disp_driver_1_a, n7_segment_disp_driver_1_b,
       n7_segment_disp_driver_1_d, n7_segment_disp_driver_1_e, n7_segment_disp_driver_1_f,
       n7_segment_disp_driver_1_g;

  Button button_1 (.out(button_1_out));
  Button button_2 (.out(button_2_out));
  Button button_3 (.out(button_3_out));
  Button button_4 (.out(button_4_out));
  Button button_5 (.out(button_5_out));
  EncodedCirc encodedcirc_1 (
    .a(button_1_out), .x(encodedcirc_1_x), .b(button_2_out), .y(encodedcirc_1_y), .c(button_3_out),
    .z(encodedcirc_1_z), .u(encodedcirc_1_u), .d(button_4_out), .e(button_5_out));
  LEDCounter_main main_1 (
    .in_1(button_1_out), .in_2(button_2_out), .in_3(button_3_out), .in_4(button_4_out), .in_5(button_5_out),
    .out_6(main_1_out_6), .out_7(main_1_out_7), .out_8(main_1_out_8), .out_9(main_1_out_9),
    .out_10(main_1_out_10));
  LED led_1 (.in(main_1_out_6));
  LED led_2 (.in(main_1_out_7));
  LED led_3 (.in(main_1_out_8));
  LED led_4 (.in(main_1_out_9));
  LED led_5 (.in(main_1_out_10));
  _7_Segment_Disp_Driver u_7_segment_disp_driver_1 (
    .In1(encodedcirc_1_x), .In2(encodedcirc_1_y), .In3(encodedcirc_1_z), .g(n7_segment_disp_driver_1_g),
    .In4(encodedcirc_1_u), .f(n7_segment_disp_driver_1_f), .a(n7_segment_disp_driver_1_a),
    .b(n7_segment_disp_driver_1_b), .e(n7_segment_disp_driver_1_e), .d(n7_segment_disp_driver_1_d),
    .c(n7_segment_disp_driver_1_d));
  _7_Segment_Display u_7_segment_display_1 (
    .g(n7_segment_disp_driver_1_g), .f(n7_segment_disp_driver_1_f), .a(n7_segment_disp_driver_1_a),
    .b(n7_segment_disp_driver_1_b), .e(n7_segment_disp_driver_1_e), .d(n7_segment_disp_driver_1_d),
    .c(n7_segment_disp_driver_1_d), .dp(1'b1));
endmodule

module EncodedCirc (
  input  a,
  input  b,
  input  c,
  input  d,
  input  e,
  output x,
  output y,
  output z,
  output u
);

  or or_1 (y, e, d);
  or or_2 (z, c, b);
  or or_3 (u, e, c, a);

  assign x = 1'b0;
endmodule

module _7_Segment_Disp_Driver (
  input  In1,
  input  In2,
  input  In3,
  input  In4,
  output g,
  output f,
  output a,
  output b,
  output e,
  output d,
  output c
);

  wire and_1_out, and_2_out, and_3_out, and_4_out, and_5_out, and_6_out, and_7_out, and_8_out, and_9_out,
       and_10_out, and_11_out, and_12_out, and_13_out, and_14_out, and_15_out, and_16_out, and_17_out,
       and_18_out, and_19_out, and_20_out, and_21_out, and_22_out, and_23_out, and_24_out, and_25_out,
       and_26_out, not_1_out, not_2_out, not_3_out, not_4_out, not_5_out, not_6_out, not_7_out, not_8_out,
       not_9_out, not_10_out, not_11_out, not_12_out, not_13_out, not_14_out, not_15_out, not_16_out,
       not_17_out, not_18_out, not_19_out, not_20_out, not_21_out, not_22_out, not_23_out, not_24_out,
       not_25_out, not_26_out, not_27_out, not_28_out, not_29_out, not_30_out, not_31_out, not_32_out,
       not_33_out, not_34_out, not_35_out, not_36_out, not_37_out, not_38_out, not_39_out, not_40_out,
       not_41_out, not_42_out, not_43_out, not_44_out, not_45_out, not_46_out, not_47_out, not_48_out,
       not_49_out, not_50_out, not_51_out, not_52_out;

  not not_1 (not_1_out, In1);
  and and_1 (and_1_out, not_1_out, not_2_out, In3);
  not not_2 (not_2_out, In2);
  not not_3 (not_3_out, In1);
  and and_2 (and_2_out, not_3_out, In2, not_4_out);
  not not_4 (not_4_out, In3);
  not not_5 (not_5_out, In1);
  and and_3 (and_3_out, not_5_out, In2, not_6_out);
  not not_6 (not_6_out, In4);
  and and_4 (and_4_out, In1, not_7_out, not_8_out);
  not not_7 (not_7_out, In2);
  not not_8 (not_8_out, In3);
  not not_9 (not_9_out, In1);
  and and_5 (and_5_out, not_9_out, not_10_out, not_11_out);
  not not_10 (not_10_out, In3);
  not not_11 (not_11_out, In4);
  not not_12 (not_12_out, In1);
  and and_6 (and_6_out, not_12_out, In2, not_13_out);
  not not_13 (not_13_out, In3);
  not not_14 (not_14_out, In1);
  and and_7 (and_7_out, not_14_out, In2, not_15_out);
  not not_15 (not_15_out, In4);
  not not_16 (not_16_out, In2);
  and and_8 (and_8_out, In1, not_16_out, not_17_out);
  not not_17 (not_17_out, In3);
  not not_18 (not_18_out, In1);
  not not_19 (not_19_out, In2);
  and and_9 (and_9_out, not_18_out, not_19_out, not_20_out);
  not not_20 (not_20_out, In4);
  not not_21 (not_21_out, In1);
  and and_10 (and_10_out, not_21_out, In3);
  not not_22 (not_22_out, In1);
  and and_11 (and_11_out, not_22_out, In2, In4);
  not not_23 (not_23_out, In2);
  and and_12 (and_12_out, In1, not_23_out, not_24_out);
  not not_24 (not_24_out, In3);
  not not_25 (not_25_out, In1);
  and and_13 (and_13_out, not_25_out, not_26_out);
  not not_26 (not_26_out, In2);
  not not_27 (not_27_out, In1);
  not not_28 (not_28_out, In3);
  and and_14 (and_14_out, not_27_out, not_28_out, not_29_out);
  not not_29 (not_29_out, In4);
  not not_30 (not_30_out, In2);
  and and_15 (and_15_out, not_30_out, not_31_out);
  not not_31 (not_31_out, In3);
  not not_32 (not_32_out, In1);
  and and_16 (and_16_out, not_32_out, In3, In4);
  not not_33 (not_33_out, In2);
  and and_17 (and_17_out, not_33_out, not_34_out, not_35_out);
  not not_34 (not_34_out, In3);
  not not_35 (not_35_out, In4);
  not not_36 (not_36_out, In1);
  and and_18 (and_18_out, not_36_out, In3, not_37_out);
  not not_37 (not_37_out, In4);
  not not_38 (not_38_out, In1);
  not not_39 (not_39_out, In2);
  not not_40 (not_40_out, In4);
  not not_41 (not_41_out, In1);
  not not_42 (not_42_out, In2);
  not not_43 (not_43_out, In1);
  not not_44 (not_44_out, In4);
  not not_45 (not_45_out, In1);
  not not_46 (not_46_out, In3);
  not not_47 (not_47_out, In2);
  not not_48 (not_48_out, In3);
  not not_49 (not_49_out, In2);
  and and_19 (and_19_out, not_49_out, not_50_out);
  not not_50 (not_50_out, In3);
  not not_51 (not_51_out, In1);
  and and_20 (and_20_out, not_51_out, In4);
  not not_52 (not_52_out, In1);
  and and_21 (and_21_out, not_52_out, In2);
  or or_1 (g, and_1_out, and_2_out, and_3_out, and_4_out);
  or or_2 (f, and_5_out, and_6_out, and_7_out, and_8_out);
  or or_3 (a, and_9_out, and_10_out, and_11_out, and_12_out);
  or or_4 (b, and_13_out, and_14_out, and_15_out, and_16_out);
  or or_5 (e, and_17_out, and_18_out);
  and and_22 (and_22_out, not_38_out, not_39_out, not_40_out);
  and and_23 (and_23_out, not_41_out, not_42_out, In3);
  and and_24 (and_24_out, not_43_out, In3, not_44_out);
  and and_25 (and_25_out, not_45_out, In2, not_46_out, In4);
  and and_26 (and_26_out, In1, not_47_out, not_48_out);
  or or_6 (c, and_19_out, and_20_out, and_21_out);
  or or_7 (d, and_22_out, and_23_out, and_24_out, and_25_out, and_26_out);
endmodule
