// Logisim project 实验7 奇校验（素材）.circ as structural Verilog
// 随机干扰
module \_9位随机干扰  (
  input  CLK,
  input  [8:0] \_9位输入 ,
  output [8:0] \随机加扰屏蔽字 ,
  output [8:0] \加扰后数据 
);

  wire [4:0] \随机数_2_out , \随机数_3_out , \随机数_out ;
  wire [8:0] or_1_out;
  wire [31:0] decoder_1_out31, decoder_2_out31, decoder_3_out31;

  Decoder #(.select(5), .enable("false")) decoder_1 (
    .out0(decoder_1_out31[31]), .out1(decoder_1_out31[30]), .out2(decoder_1_out31[29]),
    .out3(decoder_1_out31[28]), .out4(decoder_1_out31[27]), .out5(decoder_1_out31[26]),
    .out6(decoder_1_out31[25]), .out7(decoder_1_out31[24]), .out8(decoder_1_out31[23]),
    .out9(decoder_1_out31[22]), .out10(decoder_1_out31[21]), .out11(decoder_1_out31[20]),
    .out12(decoder_1_out31[19]), .out13(decoder_1_out31[18]), .out14(decoder_1_out31[17]),
    .out15(decoder_1_out31[16]), .out16(decoder_1_out31[15]), .out17(decoder_1_out31[14]),
    .out18(decoder_1_out31[13]), .out19(decoder_1_out31[12]), .out20(decoder_1_out31[11]),
    .out21(decoder_1_out31[10]), .out22(decoder_1_out31[9]), .out23(decoder_1_out31[8]),
    .out24(decoder_1_out31[7]), .out25(decoder_1_out31[6]), .out26(decoder_1_out31[5]),
    .out27(decoder_1_out31[4]), .out28(decoder_1_out31[3]), .out29(decoder_1_out31[2]),
    .out30(decoder_1_out31[1]), .out31(decoder_1_out31[0]), .sel(\随机数_out ));
  Random #(.width(5)) \u_随机数  (.clk(CLK), .out(\随机数_out ));  // open: next, clr
  Random #(.width(5), .seed(18)) \u_随机数_2  (.clk(CLK), .out(\随机数_2_out ));  // open: next, clr
  Decoder #(.select(5), .enable("false")) decoder_2 (
    .out0(decoder_2_out31[31]), .out1(decoder_2_out31[30]), .out2(decoder_2_out31[29]),
    .out3(decoder_2_out31[28]), .out4(decoder_2_out31[27]), .out5(decoder_2_out31[26]),
    .out6(decoder_2_out31[25]), .out7(decoder_2_out31[24]), .out8(decoder_2_out31[23]),
    .out9(decoder_2_out31[22]), .out10(decoder_2_out31[21]), .out11(decoder_2_out31[20]),
    .out12(decoder_2_out31[19]), .out13(decoder_2_out31[18]), .out14(decoder_2_out31[17]),
    .out15(decoder_2_out31[16]), .out16(decoder_2_out31[15]), .out17(decoder_2_out31[14]),
    .out18(decoder_2_out31[13]), .out19(decoder_2_out31[12]), .out20(decoder_2_out31[11]),
    .out21(decoder_2_out31[10]), .out22(decoder_2_out31[9]), .out23(decoder_2_out31[8]),
    .out24(decoder_2_out31[7]), .out25(decoder_2_out31[6]), .out26(decoder_2_out31[5]),
    .out27(decoder_2_out31[4]), .out28(decoder_2_out31[3]), .out29(decoder_2_out31[2]),
    .out30(decoder_2_out31[1]), .out31(decoder_2_out31[0]), .sel(\随机数_2_out ));
  Decoder #(.select(5), .enable("false")) decoder_3 (
    .out0(decoder_3_out31[31]), .out1(decoder_3_out31[30]), .out2(decoder_3_out31[29]),
    .out3(decoder_3_out31[28]), .out4(decoder_3_out31[27]), .out5(decoder_3_out31[26]),
    .out6(decoder_3_out31[25]), .out7(decoder_3_out31[24]), .out8(decoder_3_out31[23]),
    .out9(decoder_3_out31[22]), .out10(decoder_3_out31[21]), .out11(decoder_3_out31[20]),
    .out12(decoder_3_out31[19]), .out13(decoder_3_out31[18]), .out14(decoder_3_out31[17]),
    .out15(decoder_3_out31[16]), .out16(decoder_3_out31[15]), .out17(decoder_3_out31[14]),
    .out18(decoder_3_out31[13]), .out19(decoder_3_out31[12]), .out20(decoder_3_out31[11]),
    .out21(decoder_3_out31[10]), .out22(decoder_3_out31[9]), .out23(decoder_3_out31[8]),
    .out24(decoder_3_out31[7]), .out25(decoder_3_out31[6]), .out26(decoder_3_out31[5]),
    .out27(decoder_3_out31[4]), .out28(decoder_3_out31[3]), .out29(decoder_3_out31[2]),
    .out30(decoder_3_out31[1]), .out31(decoder_3_out31[0]), .sel(\随机数_3_out ));
  Random #(.width(5), .seed(3)) \u_随机数_3  (.clk(CLK), .out(\随机数_3_out ));  // open: next, clr
  assign or_1_out = decoder_1_out31[8:0] | decoder_2_out31[8:0];  // OR_Gate or_1, 9 bits wide
  assign \随机加扰屏蔽字  = or_1_out | decoder_3_out31[8:0];  // OR_Gate or_2, 9 bits wide
  assign \加扰后数据  = \随机加扰屏蔽字  ^ \_9位输入 ;  // XOR_Gate xor_1, 9 bits wide
endmodule
